// Logisim project Project 1.circ as structural Verilog
module Nand (
  input  in_1,
  input  in_2,
  output NAND
);

  wire and_1_out;

  and and_1 (and_1_out, in_1, in_2);
  not not_1 (NAND, and_1_out);
endmodule

module AND (
  input  in_1,
  input  in_2,
  output out_3
);

  wire nand_1_nand;

  Nand nand_1 (.in_1(in_1), .in_2(in_2), .NAND(nand_1_nand));
  Nand nand_2 (.in_1(nand_1_nand), .in_2(nand_1_nand), .NAND(out_3));
endmodule

module NOT (
  input  in_1,
  output A_A
);

  Nand nand_1 (.in_1(in_1), .in_2(in_1), .NAND(A_A));
endmodule

module OR (
  input  in_1,
  input  in_2,
  output out_3
);

  wire nand_1_nand, nand_3_nand;

  Nand nand_1 (.in_1(in_1), .in_2(in_1), .NAND(nand_1_nand));
  Nand nand_2 (.in_1(nand_1_nand), .in_2(nand_3_nand), .NAND(out_3));
  Nand nand_3 (.in_1(in_2), .in_2(in_2), .NAND(nand_3_nand));

  // Notes on the sheet:
  //   OR = -(-(A*A)*-(B*B))
endmodule

module ex4 (
  input  A,
  input  B,
  input  C,
  output X,
  output Y
);

  wire and_1_out, and_2_out, and_3_out, and_5_out, not_1_out, not_2_out, not_3_out, not_4_out, not_5_out,
       not_6_out, not_7_out, not_8_out, or_1_out;

  not not_1 (not_1_out, B);
  not not_2 (not_2_out, C);
  not not_3 (not_3_out, A);
  not not_4 (not_4_out, B);
  not not_5 (not_5_out, A);
  not not_6 (not_6_out, A);
  and and_1 (and_1_out, not_5_out, not_4_out);
  or or_1 (or_1_out, not_3_out, and_2_out);
  and and_2 (and_2_out, A, not_2_out);
  not not_7 (not_7_out, C);
  and and_3 (and_3_out, not_6_out, B, not_7_out);
  and and_4 (X, or_1_out, not_1_out);
  not not_8 (not_8_out, C);
  and and_5 (and_5_out, A, not_8_out);
  or or_2 (Y, and_5_out, and_3_out, and_1_out);
endmodule

module ex5 (
  input  Enable_Read,
  input  Clear,
  output [6:0] out_3
);

  wire [3:0] bit_extender_1_out;

  Hex_Digit_Display hex_digit_display_1 (.value(bit_extender_1_out));  // open: dp
  Keyboard keyboard_1 (.re(Enable_Read), .clr(Clear), .data(out_3));  // open: clk, avail
  Hex_Digit_Display hex_digit_display_2 (.value(out_3[3:0]));  // open: dp
  assign bit_extender_1_out = {{1{1'b0}}, out_3[6:4]};  // Bit_Extender bit_extender_1

  // Notes on the sheet:
  //   Splitter: From 7 to 4
  //   7 bit ASCII code
endmodule

module ex6 (
  input  [2:0] in_1
);

  wire and_1_out, and_2_out, and_3_out, and_4_out, and_5_out, and_6_out, and_7_out, and_8_out, and_9_out,
       and_10_out, and_11_out, and_12_out, and_13_out, and_14_out, and_15_out, and_16_out, and_17_out,
       and_18_out, D_out, E_out, F_out, G_out, H_out, I_out, not_1_out, not_2_out, not_3_out, not_4_out,
       not_5_out;

  not not_1 (not_1_out, in_1[2]);
  not not_2 (not_2_out, in_1[1]);
  not not_3 (not_3_out, in_1[0]);
  and and_1 (and_1_out, not_1_out, in_1[1]);
  and and_2 (and_2_out, in_1[2], not_2_out, in_1[0]);
  buf and_3 (and_3_out, in_1[1]);  // AND_Gate
  and and_4 (and_4_out, in_1[2], not_2_out, in_1[0]);
  and and_5 (and_5_out, not_1_out, not_3_out);
  and and_6 (and_6_out, not_1_out, not_3_out);
  and and_7 (and_7_out, not_3_out, in_1[2]);
  and and_8 (and_8_out, not_2_out, not_3_out);
  and and_9 (and_9_out, not_1_out, not_2_out, not_3_out);
  and and_10 (and_10_out, in_1[2], not_3_out, in_1[1]);
  and and_11 (and_11_out, in_1[2], in_1[1], not_3_out);
  and and_12 (and_12_out, not_1_out, in_1[1], in_1[0]);
  and and_13 (and_13_out, not_1_out, in_1[1], not_3_out);
  and and_14 (and_14_out, in_1[0], in_1[2], not_2_out);
  and and_15 (and_15_out, in_1[2], in_1[1], not_3_out);
  and and_16 (and_16_out, in_1[2], not_2_out, in_1[0]);
  and and_17 (and_17_out, in_1[2], in_1[1], not_3_out);
  or D (D_out, and_14_out, and_7_out, and_1_out);
  or E (E_out, and_15_out, and_8_out, and_2_out);
  or F (F_out, and_16_out, and_9_out, and_3_out);
  not not_4 (not_4_out, G_out);
  or G (G_out, and_10_out, and_4_out);
  or H (H_out, and_11_out, and_5_out);
  and and_18 (and_18_out, in_1[2], not_2_out, in_1[0]);
  _7_Segment_Display u_7_segment_display_1 (
    .g(D_out), .f(E_out), .a(F_out), .b(not_4_out), .e(H_out), .d(I_out), .c(not_5_out));  // open: dp
  or I (I_out, and_18_out, and_17_out, and_12_out, and_6_out);
  not not_5 (not_5_out, and_13_out);

  // Notes on the sheet:
  //   C
  //   B
  //   A
endmodule
