// Logisim project ALU_Group50.circ as structural Verilog: 16 circuits, main circuit main
module main (
  output halt,
  output [6:0] counter,
  output [3:0] op,
  output [7:0] a,
  output [7:0] b,
  output [7:0] oracle,
  output [7:0] result,
  output err_oracle,
  output error,
  output ok,
  output start_delimiter
);

  wire and_1_out, and_2_out, clock_1_out, comparator_1_eq, comparator_2_eq;

  Clock clock_1 (.out(clock_1_out));
  Counter #(.width(7), .max('h7f), .trigger("falling")) counter_1 (
    .Q(counter), .carry(halt), .clk(clock_1_out));  // open: load, D, count, clr
  RAM #(.addrWidth(10), .dataWidth(4), .bus("separate")) ram_1 (
    .addr({counter, 3'b000}), .data(op), .ld(1'b1));  // open: din, str, sel, clk, clr
  RAM #(.addrWidth(10), .bus("separate")) ram_2 (
    .addr({counter, 3'b001}), .data(a), .ld(1'b1));  // open: din, str, sel, clk, clr
  RAM #(.addrWidth(10), .bus("separate")) ram_3 (
    .addr({counter, 3'b010}), .data(b), .ld(1'b1));  // open: din, str, sel, clk, clr
  RAM #(.addrWidth(10), .bus("separate")) ram_4 (
    .addr({counter, 3'b011}), .data(oracle), .ld(1'b1));  // open: din, str, sel, clk, clr
  RAM #(.addrWidth(10), .dataWidth(1), .bus("separate")) ram_5 (
    .addr({counter, 3'b100}), .data(err_oracle), .ld(1'b1));  // open: din, str, sel, clk, clr
  RAM #(.addrWidth(10), .dataWidth(1), .bus("separate")) ram_6 (
    .addr({counter, 3'b101}), .data(start_delimiter), .ld(1'b1));  // open: din, str, sel, clk, clr
  _8_bit_ALU u_8_bit_alu_1 (.ALU_code(op), .a(a), .b(b), .result(result), .overflow(error));
  Comparator #(.width(1), .mode("unsigned")) comparator_1 (
    .a(error), .b(err_oracle), .eq(comparator_1_eq));  // open: gt, lt
  Comparator comparator_2 (.a(result), .b(oracle), .eq(comparator_2_eq));  // open: gt, lt
  and and_1 (and_1_out, comparator_1_eq, error);
  and and_2 (and_2_out, comparator_2_eq, comparator_1_eq, ~error);  // AND_Gate
  or or_1 (ok, and_1_out, and_2_out);

  // Notes on the sheet:
  //   You must complete the circuit '8-bit ALU' instead.
  //   DO NOT EDIT THIS CIRCUIT!
  //   LT, GT, Sub, shift
endmodule

module _8_bit_ALU (
  input  [3:0] ALU_code,
  input  [7:0] a,
  input  [7:0] b,
  output overflow,
  output [7:0] result
);

  wire add_1_out_4, inverse_1_out_3, sla_1_out_3, sra_1_out_3, sub_1_out_4;
  wire [7:0] add_1_out_3, and_1_out, eq_1_out_3, generate_zero_1_out_1, gt_1_out_3, inverse_1_out_2,
       lt_1_out_3, neq_1_out_3, not_1_out_2, or_1_out_3, shift_left_logical_1_out_2,
       shift_right_logical_1_out_2, sla_1_out_2, sra_1_out_2, sub_1_out_3;

  Multiplexer #(.select(4)) multiplexer_1 (
    .in0(1'b0), .in1(1'b0), .in2(1'b0), .in3(1'b0), .in4(add_1_out_4), .in5(sub_1_out_4), .in6(1'b0),
    .in7(1'b0), .in8(1'b0), .in9(1'b0), .in10(inverse_1_out_3), .in11(1'b0), .in12(1'b0), .in13(sla_1_out_3),
    .in14(sra_1_out_3), .in15(1'b0), .out(overflow), .sel(ALU_code));  // open: en
  Multiplexer #(.select(4), .width(8)) multiplexer_2 (
    .in0(generate_zero_1_out_1), .in1(not_1_out_2), .in2(and_1_out), .in3(or_1_out_3), .in4(add_1_out_3),
    .in5(sub_1_out_3), .in6(lt_1_out_3), .in7(gt_1_out_3), .in8(eq_1_out_3), .in9(neq_1_out_3),
    .in10(inverse_1_out_2), .in11(shift_left_logical_1_out_2), .in12(shift_right_logical_1_out_2),
    .in13(sla_1_out_2), .in14(sra_1_out_2), .in15(a), .out(result), .sel(ALU_code));  // open: en
  assign and_1_out = b & a;  // AND_Gate and_1, 8 bits wide
  Generate_Zero generate_zero_1 (.out_1(generate_zero_1_out_1));
  SUB sub_1 (.in_1(a), .in_2(b), .out_3(sub_1_out_3), .out_4(sub_1_out_4));
  Inverse inverse_1 (.in_1(a), .out_2(inverse_1_out_2), .out_3(inverse_1_out_3));
  NOT not_1 (.out_2(not_1_out_2), .in_1(a));
  OR or_1 (.out_3(or_1_out_3), .in_1(a), .in_2(b));
  ADD add_1 (.out_3(add_1_out_3), .out_4(add_1_out_4), .in_1(a), .in_2(b));
  LT lt_1 (.out_3(lt_1_out_3), .in_1(a), .in_2(b));
  GT gt_1 (.out_3(gt_1_out_3), .in_1(a), .in_2(b));
  EQ eq_1 (.out_3(eq_1_out_3), .in_1(a), .in_2(b));
  NEQ neq_1 (.out_3(neq_1_out_3), .in_1(a), .in_2(b));
  shift_left_logical shift_left_logical_1 (.out_2(shift_left_logical_1_out_2), .in_1(a));
  shift_right_logical shift_right_logical_1 (.out_2(shift_right_logical_1_out_2), .in_1(a));
  sla sla_1 (.out_2(sla_1_out_2), .out_3(sla_1_out_3), .in_1(a));
  sra sra_1 (.out_2(sra_1_out_2), .out_3(sra_1_out_3), .in_1(a));

  // Notes on the sheet:
  //   This circuit is used as a block in the main circuit, and its layout must remain unchanged. The circuit called "main" should be the main circuit of this file.
  //   Do not change the circuit appearance.
  //   DO NOT CHANGE THE INPUTS AND OUTPUTS OF THIS CIRCUIT!
  //   Do not add/remove inputs or outputs. Do not even change their location or orientation.
endmodule

module Generate_Zero (
  output [7:0] out_1
);


  assign out_1 = {8{1'b0}};
endmodule

module NOT (
  input  [7:0] in_1,
  output [7:0] out_2
);

  assign out_2 = ~in_1;  // NOT_Gate not_1, 8 bits wide
endmodule

module OR (
  input  [7:0] in_1,
  input  [7:0] in_2,
  output [7:0] out_3
);

  assign out_3 = in_1 | in_2;  // OR_Gate or_1, 8 bits wide
endmodule

module ADD (
  input  [7:0] in_1,
  input  [7:0] in_2,
  output [7:0] out_3,
  output out_4
);

  real_8_bit_CLA real_8_bit_cla_1 (.in_1(in_2), .in_2(in_1), .out_3(out_3), .out_4(out_4));
endmodule

module SUB (
  input  [7:0] in_1,
  input  [7:0] in_2,
  output [7:0] out_3,
  output out_4
);

  wire add_1_out_4, inverse_1_out_3;
  wire [7:0] inverse_1_out_2;

  or or_1 (out_4, add_1_out_4, inverse_1_out_3);
  ADD add_1 (.out_3(out_3), .out_4(add_1_out_4), .in_1(in_1), .in_2(inverse_1_out_2));
  Inverse inverse_1 (.in_1(in_2), .out_2(inverse_1_out_2), .out_3(inverse_1_out_3));

  // Notes on the sheet:
  //   Overflow fixen!!!!!!: Done, should work now
endmodule

module Inverse (
  input  [7:0] in_1,
  output [7:0] out_2,
  output out_3
);

  wire [7:0] not_1_out_2;

  ADD add_1 (.out_3(out_2), .out_4(out_3), .in_1(not_1_out_2), .in_2(8'h1));
  NOT not_1 (.out_2(not_1_out_2), .in_1(in_1));
endmodule

module LT (
  input  [7:0] in_1,
  input  [7:0] in_2,
  output [7:0] out_3
);

  wire and_1_out, multiplexer_1_out, not_1_out, sub_1_out_4;
  wire [7:0] sub_1_out_3;

  Multiplexer multiplexer_1 (
    .in0(sub_1_out_3[7]), .in1(and_1_out), .out(multiplexer_1_out), .sel(sub_1_out_4));  // open: en
  and and_1 (and_1_out, not_1_out, in_1[7]);
  assign out_3 = {{7{1'b0}}, multiplexer_1_out};  // Bit_Extender bit_extender_1
  not not_1 (not_1_out, in_2[7]);
  SUB sub_1 (.in_1(in_1), .in_2(in_2), .out_3(sub_1_out_3), .out_4(sub_1_out_4));

  // Notes on the sheet:
  //   A < B <=> B-A > 0
endmodule

module GT (
  input  [7:0] in_1,
  input  [7:0] in_2,
  output [7:0] out_3
);

  wire and_1_out, multiplexer_1_out, not_1_out, sub_1_out_4;
  wire [7:0] sub_1_out_3;

  Multiplexer multiplexer_1 (
    .in0(sub_1_out_3[7]), .in1(and_1_out), .out(multiplexer_1_out), .sel(sub_1_out_4));  // open: en
  and and_1 (and_1_out, not_1_out, in_2[7]);
  assign out_3 = {{7{1'b0}}, multiplexer_1_out};  // Bit_Extender bit_extender_1
  not not_1 (not_1_out, in_1[7]);
  SUB sub_1 (.in_1(in_2), .in_2(in_1), .out_3(sub_1_out_3), .out_4(sub_1_out_4));
endmodule

module EQ (
  input  [7:0] in_1,
  input  [7:0] in_2,
  output [7:0] out_3
);

  wire and_1_out, and_2_out, not_1_out, not_2_out, not_3_out, not_4_out, or_1_out, or_2_out, or_3_out,
       sub_1_out_4, sub_2_out_4;
  wire [7:0] sub_1_out_3, sub_2_out_3;

  or or_1 (or_1_out, and_1_out, and_2_out);
  assign out_3 = {{7{1'b0}}, or_1_out};  // Bit_Extender bit_extender_1
  and and_1 (and_1_out, not_1_out, not_2_out);
  and and_2 (and_2_out, not_3_out, not_4_out);
  not not_1 (not_1_out, or_3_out);
  not not_2 (not_2_out, sub_2_out_4);
  not not_3 (not_3_out, or_2_out);
  or or_2 (or_2_out, sub_1_out_3[0], sub_1_out_3[1], sub_1_out_3[2], sub_1_out_3[3], sub_1_out_3[4], sub_1_out_3[5], sub_1_out_3[6], sub_1_out_3[7]);
  not not_4 (not_4_out, sub_1_out_4);
  or or_3 (or_3_out, sub_2_out_3[0], sub_2_out_3[1], sub_2_out_3[2], sub_2_out_3[3], sub_2_out_3[4], sub_2_out_3[5], sub_2_out_3[6], sub_2_out_3[7]);
  SUB sub_1 (.in_1(in_2), .in_2(in_1), .out_3(sub_1_out_3), .out_4(sub_1_out_4));
  SUB sub_2 (.in_1(in_1), .in_2(in_2), .out_3(sub_2_out_3), .out_4(sub_2_out_4));

  // Notes on the sheet:
  //   If one of the substracts gives overflow, the other should give the right result
endmodule

module NEQ (
  input  [7:0] in_1,
  input  [7:0] in_2,
  output [7:0] out_3
);

  wire not_1_out;
  wire [7:0] eq_1_out_3;

  assign out_3 = {{7{1'b0}}, not_1_out};  // Bit_Extender bit_extender_1
  not not_1 (not_1_out, eq_1_out_3[0]);
  EQ eq_1 (.out_3(eq_1_out_3), .in_1(in_1), .in_2(in_2));
endmodule

module shift_left_logical (
  input  [7:0] in_1,
  output [7:0] out_2
);


  assign out_2 = {in_1[6:0], 1'b0};
endmodule

module shift_right_logical (
  input  [7:0] in_1,
  output [7:0] out_2
);


  assign out_2 = {1'b0, in_1[7:1]};
endmodule

module sla (
  input  [7:0] in_1,
  output [7:0] out_2,
  output out_3
);

  wire and_1_out, and_2_out, not_2_out;

  buf and_1 (and_1_out, in_1[7]);  // AND_Gate
  or or_1 (out_3, and_1_out, and_2_out);
  and and_2 (and_2_out, in_1[6], not_2_out);
  // NOT_Gate not_1 has open pins: in=in_1[6], out=open
  not not_2 (not_2_out, in_1[7]);

  assign out_2 = {in_1[6:0], 1'b0};

  // Notes on the sheet:
  //   Eerste bit checken
endmodule

module sra (
  input  [7:0] in_1,
  output [7:0] out_2,
  output out_3
);

  wire and_1_out, and_2_out, not_2_out;

  buf and_1 (and_1_out, in_1[7]);  // AND_Gate
  // NOT_Gate not_1 has open pins: in=1'b0, out=open
  or or_1 (out_3, and_1_out, and_2_out);
  and and_2 (and_2_out, 1'b0, not_2_out);
  not not_2 (not_2_out, in_1[7]);

  assign out_2 = {1'b0, in_1[7:1]};

  // Notes on the sheet:
  //   Sign toevoegen vanvoor, nooit overflow
endmodule
