// Logisim project Project 2.circ as structural Verilog
module Decoder (
  input  [2:0] in_1,
  output out_2,
  output out_3,
  output out_4,
  output out_5,
  output out_6,
  output out_7,
  output out_8,
  output out_9
);

  wire not_1_out, not_2_out, not_3_out;

  not not_1 (not_1_out, in_1[0]);
  not not_2 (not_2_out, in_1[1]);
  not not_3 (not_3_out, in_1[2]);
  and and_1 (out_9, in_1[2], in_1[1], in_1[0]);
  and and_2 (out_8, not_3_out, in_1[1], in_1[0]);
  and and_3 (out_7, in_1[2], not_2_out, in_1[0]);
  and and_4 (out_5, in_1[2], in_1[1], not_1_out);
  and and_5 (out_6, not_3_out, not_2_out, in_1[0]);
  and and_6 (out_3, in_1[2], not_2_out, not_1_out);
  and and_7 (out_2, not_3_out, not_2_out, not_1_out);
  and and_8 (out_4, not_3_out, in_1[1], not_1_out);
endmodule

module Multiplexer (
  input  [7:0] in_1,
  input  [7:0] in_2,
  input  [7:0] in_3,
  input  [7:0] in_4,
  input  [7:0] in_5,
  input  [7:0] in_6,
  input  [7:0] in_7,
  input  [7:0] in_8,
  input  [2:0] in_9,
  output [7:0] out_10
);

  wire decoder_1_out_2, decoder_1_out_3, decoder_1_out_4, decoder_1_out_5, decoder_1_out_6, decoder_1_out_7,
       decoder_1_out_8, decoder_1_out_9;
  wire [7:0] and_1_out, and_2_out, and_3_out, and_4_out, and_5_out, and_6_out, and_7_out, and_8_out,
       bit_extender_1_out, bit_extender_2_out, bit_extender_3_out, bit_extender_4_out, bit_extender_5_out,
       bit_extender_6_out, bit_extender_7_out, bit_extender_8_out;

  Decoder decoder_1 (
    .in_1(in_9), .out_2(decoder_1_out_2), .out_3(decoder_1_out_3), .out_4(decoder_1_out_4),
    .out_5(decoder_1_out_5), .out_6(decoder_1_out_6), .out_7(decoder_1_out_7), .out_8(decoder_1_out_8),
    .out_9(decoder_1_out_9));
  assign and_1_out = in_1 & bit_extender_1_out;  // AND_Gate and_1, 8 bits wide
  assign bit_extender_1_out = {{7{decoder_1_out_2}}, decoder_1_out_2};  // Bit_Extender bit_extender_1
  assign and_2_out = in_2 & bit_extender_2_out;  // AND_Gate and_2, 8 bits wide
  assign bit_extender_2_out = {{7{decoder_1_out_3}}, decoder_1_out_3};  // Bit_Extender bit_extender_2
  assign and_3_out = in_3 & bit_extender_3_out;  // AND_Gate and_3, 8 bits wide
  assign bit_extender_3_out = {{7{decoder_1_out_4}}, decoder_1_out_4};  // Bit_Extender bit_extender_3
  assign and_4_out = in_4 & bit_extender_4_out;  // AND_Gate and_4, 8 bits wide
  assign bit_extender_4_out = {{7{decoder_1_out_5}}, decoder_1_out_5};  // Bit_Extender bit_extender_4
  assign and_5_out = in_5 & bit_extender_5_out;  // AND_Gate and_5, 8 bits wide
  assign bit_extender_5_out = {{7{decoder_1_out_6}}, decoder_1_out_6};  // Bit_Extender bit_extender_5
  assign and_6_out = in_6 & bit_extender_6_out;  // AND_Gate and_6, 8 bits wide
  assign bit_extender_6_out = {{7{decoder_1_out_7}}, decoder_1_out_7};  // Bit_Extender bit_extender_6
  assign and_7_out = in_7 & bit_extender_7_out;  // AND_Gate and_7, 8 bits wide
  assign bit_extender_7_out = {{7{decoder_1_out_8}}, decoder_1_out_8};  // Bit_Extender bit_extender_7
  assign and_8_out = in_8 & bit_extender_8_out;  // AND_Gate and_8, 8 bits wide
  assign bit_extender_8_out = {{7{decoder_1_out_9}}, decoder_1_out_9};  // Bit_Extender bit_extender_8
  assign out_10 = and_1_out | and_2_out | and_3_out | and_4_out | and_5_out | and_6_out | and_7_out | and_8_out;  // OR_Gate or_1, 8 bits wide

  // Notes on the sheet:
  //   Latency: 2e
  //   (Extender has latency 1e)
endmodule

module _1_bit_adder (
  input  Carry_in,
  input  A,
  input  B,
  output Carry_out,
  output Sum
);

  wire and_1_out, and_2_out, and_3_out, and_4_out, and_5_out, and_6_out, and_7_out, not_1_out, not_2_out,
       not_3_out;

  not not_1 (not_1_out, Carry_in);
  not not_2 (not_2_out, A);
  not not_3 (not_3_out, B);
  and and_1 (and_1_out, B, A);
  and and_2 (and_2_out, Carry_in, not_2_out, not_3_out);
  and and_3 (and_3_out, B, Carry_in);
  and and_4 (and_4_out, not_1_out, A, not_3_out);
  and and_5 (and_5_out, A, Carry_in);
  and and_6 (and_6_out, not_1_out, not_2_out, B);
  or or_1 (Carry_out, and_5_out, and_3_out, and_1_out);
  and and_7 (and_7_out, Carry_in, A, B);
  or or_2 (Sum, and_7_out, and_6_out, and_4_out, and_2_out);
endmodule

module _8_bit_ripple_carry_adder (
  input  [7:0] in_1,
  input  [7:0] in_2,
  output [7:0] out_3,
  output overflow
);

  wire n1_bit_adder_1_carry_out, n1_bit_adder_2_carry_out, n1_bit_adder_3_carry_out,
       n1_bit_adder_4_carry_out, n1_bit_adder_5_carry_out, n1_bit_adder_6_carry_out, n1_bit_adder_7_carry_out;

  _1_bit_adder u_1_bit_adder_1 (
    .Carry_in(1'b0), .A(in_1[0]), .B(in_2[0]), .Carry_out(n1_bit_adder_1_carry_out), .Sum(out_3[0]));
  _1_bit_adder u_1_bit_adder_2 (
    .Carry_in(n1_bit_adder_1_carry_out), .A(in_1[1]), .B(in_2[1]), .Carry_out(n1_bit_adder_2_carry_out),
    .Sum(out_3[1]));
  _1_bit_adder u_1_bit_adder_3 (
    .Carry_in(n1_bit_adder_2_carry_out), .A(in_1[2]), .B(in_2[2]), .Carry_out(n1_bit_adder_3_carry_out),
    .Sum(out_3[2]));
  _1_bit_adder u_1_bit_adder_4 (
    .Carry_in(n1_bit_adder_3_carry_out), .A(in_1[3]), .B(in_2[3]), .Carry_out(n1_bit_adder_4_carry_out),
    .Sum(out_3[3]));
  _1_bit_adder u_1_bit_adder_5 (
    .Carry_in(n1_bit_adder_4_carry_out), .A(in_1[4]), .B(in_2[4]), .Carry_out(n1_bit_adder_5_carry_out),
    .Sum(out_3[4]));
  _1_bit_adder u_1_bit_adder_6 (
    .Carry_in(n1_bit_adder_5_carry_out), .A(in_1[5]), .B(in_2[5]), .Carry_out(n1_bit_adder_6_carry_out),
    .Sum(out_3[5]));
  _1_bit_adder u_1_bit_adder_7 (
    .Carry_in(n1_bit_adder_6_carry_out), .A(in_1[6]), .B(in_2[6]), .Carry_out(n1_bit_adder_7_carry_out),
    .Sum(out_3[6]));
  _1_bit_adder u_1_bit_adder_8 (
    .Carry_in(n1_bit_adder_7_carry_out), .A(in_1[7]), .B(in_2[7]), .Sum(out_3[7]));  // open: Carry_out
  overflow_checker overflow_checker_1 (
    .eerste_bit_A(in_1[7]), .eerste_bit_B(in_2[7]), .Sum(out_3[7]), .Overflow(overflow));

  // Notes on the sheet:
  //   Carry Out = Overflow
  //   Sum
endmodule

module _4_bit_CLA (
  input  c0,
  input  [3:0] A,
  input  [3:0] B,
  output [3:0] S,
  output P0,
  output G0
);

  wire c1_out, c2_out, c3_out, g0_out, g1_out, g2_out, g3_out, p0_c0_out, p0_out, p1_g0_out, p1_out,
       p1_p0_c0_out, p2_g1_out, p2_out, p2_p1_g0_out, p2_p1_p0_c0_out, p3_g2_out, p3_out, p3_p2_g1_out,
       p3_p2_p1_g0_out;

  and u_g0 (g0_out, A[0], B[0]);
  or u_p0 (p0_out, A[0], B[0]);
  and g1 (g1_out, A[1], B[1]);
  or p1 (p1_out, A[1], B[1]);
  and g2 (g2_out, B[2], A[2]);
  or p2 (p2_out, B[2], A[2]);
  and g3 (g3_out, A[3], B[3]);
  or p3 (p3_out, A[3], B[3]);
  and p0_c0 (p0_c0_out, c0, p0_out);
  and p1_g0 (p1_g0_out, g0_out, p1_out);
  and p1_p0_c0 (p1_p0_c0_out, c0, p0_out, p1_out);
  and p2_g1 (p2_g1_out, g1_out, p2_out);
  and p2_p1_g0 (p2_p1_g0_out, g0_out, p1_out, p2_out);
  and p2_p1_p0_c0 (p2_p1_p0_c0_out, p2_out, p1_out, c0, p0_out);
  or c1 (c1_out, g0_out, p0_c0_out);
  or c2 (c2_out, p1_g0_out, p1_p0_c0_out, g1_out);
  or c3 (c3_out, p2_g1_out, p2_p1_g0_out, p2_p1_p0_c0_out, g2_out);
  and P0_2 (P0, p2_out, p0_out, p1_out, p3_out);
  and p3_g2 (p3_g2_out, p3_out, g2_out);
  and p3_p2_g1 (p3_p2_g1_out, p3_out, p2_out, g1_out);
  and p3_p2_p1_g0 (p3_p2_p1_g0_out, p3_out, p2_out, p1_out, g0_out);
  or G0_2 (G0, g3_out, p3_g2_out, p3_p2_g1_out, p3_p2_p1_g0_out);
  _1_bit_adder u_1_bit_adder_1 (.Carry_in(c0), .A(A[0]), .B(B[0]), .Sum(S[0]));  // open: Carry_out
  _1_bit_adder u_1_bit_adder_2 (.Carry_in(c1_out), .A(A[1]), .B(B[1]), .Sum(S[1]));  // open: Carry_out
  _1_bit_adder u_1_bit_adder_3 (.Carry_in(c2_out), .A(A[2]), .B(B[2]), .Sum(S[2]));  // open: Carry_out
  _1_bit_adder u_1_bit_adder_4 (.Carry_in(c3_out), .A(A[3]), .B(B[3]), .Sum(S[3]));  // open: Carry_out
endmodule

module _8_bit_CLA (
  input  c0,
  input  [3:0] in_2,
  input  [3:0] in_3,
  input  [3:0] in_4,
  input  [3:0] in_5,
  output [3:0] out_6,
  output [3:0] out_7
);

  wire carry_lookahead_unit_1_out_4, n4_bit_cla_2_g0, n4_bit_cla_2_p0;

  _4_bit_CLA u_4_bit_cla_1 (.c0(carry_lookahead_unit_1_out_4), .A(in_2), .B(in_3), .S(out_6));  // open: P0, G0
  carry_lookahead_unit carry_lookahead_unit_1 (
    .c0(c0), .out_4(carry_lookahead_unit_1_out_4), .G0(n4_bit_cla_2_g0), .P0(n4_bit_cla_2_p0));
  _4_bit_CLA u_4_bit_cla_2 (.c0(c0), .A(in_4), .B(in_5), .S(out_7), .P0(n4_bit_cla_2_p0), .G0(n4_bit_cla_2_g0));
endmodule

module carry_lookahead_unit (
  input  c0,
  input  G0,
  input  P0,
  output out_4
);

  wire and_1_out;

  or or_1 (out_4, G0, and_1_out);
  and and_1 (and_1_out, P0, c0);
endmodule

module real_8_bit_CLA (
  input  [7:0] in_1,
  input  [7:0] in_2,
  output [7:0] out_3,
  output out_4
);

  _8_bit_CLA u_8_bit_cla_1 (
    .out_6(out_3[7:4]), .in_3(in_1[7:4]), .in_2(in_2[7:4]), .out_7(out_3[3:0]), .in_5(in_1[3:0]),
    .in_4(in_2[3:0]), .c0(1'b0));
  overflow_checker overflow_checker_1 (
    .eerste_bit_A(in_1[7]), .eerste_bit_B(in_2[7]), .Sum(out_3[7]), .Overflow(out_4));
endmodule

module overflow_checker (
  input  eerste_bit_A,
  input  eerste_bit_B,
  input  Sum,
  output Overflow
);

  wire and_1_out, and_2_out, not_1_out, not_2_out, not_3_out;

  not not_1 (not_1_out, Sum);
  not not_2 (not_2_out, eerste_bit_A);
  not not_3 (not_3_out, eerste_bit_B);
  and and_1 (and_1_out, not_1_out, eerste_bit_A, eerste_bit_B);
  and and_2 (and_2_out, not_2_out, not_3_out, Sum);
  or or_1 (Overflow, and_1_out, and_2_out);
endmodule

module Ripple_vs_CLA (
  input  [7:0] in_1,
  input  [7:0] in_2,
  output [7:0] out_3,
  output out_4,
  output [7:0] out_5,
  output out_6
);

  _8_bit_ripple_carry_adder u_8_bit_ripple_carry_adder_1 (.in_1(in_1), .in_2(in_2), .out_3(out_3), .overflow(out_4));
  real_8_bit_CLA real_8_bit_cla_1 (.in_1(in_1), .in_2(in_2), .out_3(out_5), .out_4(out_6));
endmodule
