// Logisim project Project 4.circ as structural Verilog
module _8_bit_Registry (
  input  [7:0] D,
  input  C,
  input  Reset,
  input  Write,
  output [7:0] Q
);

  D_Flip_Flop d_ff_1 (.clk(C), .D(D[0]), .Q(Q[0]), .en(Write), .reset(Reset));  // open: Qn, preset
  D_Flip_Flop d_ff_2 (.clk(C), .D(D[1]), .Q(Q[1]), .en(Write), .reset(Reset));  // open: Qn, preset
  D_Flip_Flop d_ff_3 (.clk(C), .D(D[2]), .Q(Q[2]), .en(Write), .reset(Reset));  // open: Qn, preset
  D_Flip_Flop d_ff_4 (.clk(C), .D(D[3]), .Q(Q[3]), .en(Write), .reset(Reset));  // open: Qn, preset
  D_Flip_Flop d_ff_5 (.clk(C), .D(D[4]), .Q(Q[4]), .en(Write), .reset(Reset));  // open: Qn, preset
  D_Flip_Flop d_ff_6 (.clk(C), .D(D[5]), .Q(Q[5]), .en(Write), .reset(Reset));  // open: Qn, preset
  D_Flip_Flop d_ff_7 (.clk(C), .D(D[6]), .Q(Q[6]), .en(Write), .reset(Reset));  // open: Qn, preset
  D_Flip_Flop d_ff_8 (.clk(C), .D(D[7]), .Q(Q[7]), .en(Write), .reset(Reset));  // open: Qn, preset
endmodule

module Counter (
  input  [7:0] D,
  input  C,
  output [7:0] out_3
);

  wire comparator_1_lt, not_1_out, not_2_out;
  wire [7:0] undriven;

  _8_bit_Registry u_8_bit_registry_1 (.D(undriven), .C(C), .Reset(not_1_out), .Write(not_2_out), .Q(out_3));
  Comparator comparator_1 (.a(out_3), .b(D), .lt(comparator_1_lt));  // open: gt, eq
  not not_1 (not_1_out, comparator_1_lt);
  // NOT_Gate not_2 has open pins: in=open, out=not_2_out
endmodule

module State_traffic_light (
  input  C
);

  wire clock_1_out, comparator_1_eq, comparator_2_eq, decoder_1_out0, decoder_1_out1, decoder_1_out2,
       decoder_2_out0, decoder_2_out1, decoder_2_out2, decoder_2_out3, or_1_out;
  wire [1:0] bit_extender_1_out, bit_extender_2_out;
  wire [7:0] counter_1_out_3, counter_2_out_3, multiplexer_1_out, multiplexer_2_out, Time_Counter_2_out_3,
       Time_Counter_out_3;

  Clock clock_1 (.out(clock_1_out));
  Multiplexer #(.select(2), .width(8)) multiplexer_1 (
    .in0(8'h10), .in1(8'h8), .in2(8'h20), .out(multiplexer_1_out), .sel(bit_extender_1_out));  // open: in3, en
  Counter Time_Counter (.D(multiplexer_1_out), .C(clock_1_out), .out_3(Time_Counter_out_3));
  Multiplexer #(.select(2), .width(8)) multiplexer_2 (
    .in0(8'h1c), .in1(8'h10), .in2(8'h8), .in3(8'h4), .out(multiplexer_2_out), .sel(bit_extender_2_out));  // open: en
  Counter Time_Counter_2 (.D(multiplexer_2_out), .C(clock_1_out), .out_3(Time_Counter_2_out_3));
  Comparator comparator_1 (.a(Time_Counter_out_3), .b({8{1'b0}}), .eq(comparator_1_eq));  // open: gt, lt
  Comparator comparator_2 (.a(Time_Counter_2_out_3), .b({8{1'b0}}), .eq(comparator_2_eq));  // open: gt, lt
  Bit_Extender #(.out_width(2)) bit_extender_1 (.in(counter_1_out_3), .out(bit_extender_1_out));
  Counter counter_1 (.D(8'h3), .C(comparator_1_eq), .out_3(counter_1_out_3));
  Bit_Extender #(.out_width(2)) bit_extender_2 (.in(counter_2_out_3), .out(bit_extender_2_out));
  Counter counter_2 (.D(8'h4), .C(comparator_2_eq), .out_3(counter_2_out_3));
  LED led_1 (.in(decoder_1_out2));
  Decoder #(.select(2)) decoder_1 (
    .out0(decoder_1_out0), .out1(decoder_1_out1), .out2(decoder_1_out2), .sel(bit_extender_1_out));  // open: out3, en
  LED led_2 (.in(decoder_1_out1));
  LED led_3 (.in(decoder_1_out0));
  Decoder #(.select(2)) decoder_2 (
    .out0(decoder_2_out0), .out1(decoder_2_out1), .out2(decoder_2_out2), .out3(decoder_2_out3),
    .sel(bit_extender_2_out));  // open: en
  or or_1 (or_1_out, decoder_2_out0, decoder_2_out3);
  LED led_4 (.in(or_1_out));
  LED led_5 (.in(decoder_2_out2));
  LED led_6 (.in(decoder_2_out1));

  // Notes on the sheet:
  //   Light 1
  //   Light 2
endmodule

module Register_file (
  input  [3:0] rs_in,
  input  [3:0] rt_in,
  input  [7:0] \input ,
  input  [3:0] in_4,
  input  clock,
  input  reset,
  input  write,
  output [7:0] rs_content,
  output [7:0] rt_content
);

  wire [7:0] demultiplexer_1_out0, demultiplexer_1_out1, demultiplexer_1_out2, demultiplexer_1_out3,
       demultiplexer_1_out4, demultiplexer_1_out5, demultiplexer_1_out6, demultiplexer_1_out7,
       demultiplexer_1_out8, demultiplexer_1_out9, demultiplexer_1_out10, demultiplexer_1_out11,
       demultiplexer_1_out12, demultiplexer_1_out13, demultiplexer_1_out14, demultiplexer_1_out15,
       n8_bit_registry_1_q, n8_bit_registry_2_q, n8_bit_registry_3_q, n8_bit_registry_4_q,
       n8_bit_registry_5_q, n8_bit_registry_6_q, n8_bit_registry_7_q, n8_bit_registry_8_q,
       n8_bit_registry_9_q, n8_bit_registry_10_q, n8_bit_registry_11_q, n8_bit_registry_12_q,
       n8_bit_registry_13_q, n8_bit_registry_14_q, n8_bit_registry_15_q, n8_bit_registry_16_q;

  Demultiplexer #(.select(4), .width(8)) demultiplexer_1 (
    .out0(demultiplexer_1_out0), .out1(demultiplexer_1_out1), .out2(demultiplexer_1_out2),
    .out3(demultiplexer_1_out3), .out4(demultiplexer_1_out4), .out5(demultiplexer_1_out5),
    .out6(demultiplexer_1_out6), .out7(demultiplexer_1_out7), .out8(demultiplexer_1_out8),
    .out9(demultiplexer_1_out9), .out10(demultiplexer_1_out10), .out11(demultiplexer_1_out11),
    .out12(demultiplexer_1_out12), .out13(demultiplexer_1_out13), .out14(demultiplexer_1_out14),
    .out15(demultiplexer_1_out15), .in(\input ), .sel(in_4));  // open: en
  _8_bit_Registry u_8_bit_registry_1 (
    .D(demultiplexer_1_out0), .C(clock), .Reset(reset), .Write(write), .Q(n8_bit_registry_1_q));
  _8_bit_Registry u_8_bit_registry_2 (
    .D(demultiplexer_1_out1), .C(clock), .Reset(reset), .Write(write), .Q(n8_bit_registry_2_q));
  _8_bit_Registry u_8_bit_registry_3 (
    .D(demultiplexer_1_out2), .C(clock), .Reset(reset), .Write(write), .Q(n8_bit_registry_3_q));
  _8_bit_Registry u_8_bit_registry_4 (
    .D(demultiplexer_1_out3), .C(clock), .Reset(reset), .Write(write), .Q(n8_bit_registry_4_q));
  _8_bit_Registry u_8_bit_registry_5 (
    .D(demultiplexer_1_out4), .C(clock), .Reset(reset), .Write(write), .Q(n8_bit_registry_5_q));
  _8_bit_Registry u_8_bit_registry_6 (
    .D(demultiplexer_1_out5), .C(clock), .Reset(reset), .Write(write), .Q(n8_bit_registry_6_q));
  _8_bit_Registry u_8_bit_registry_7 (
    .D(demultiplexer_1_out6), .C(clock), .Reset(reset), .Write(write), .Q(n8_bit_registry_7_q));
  _8_bit_Registry u_8_bit_registry_8 (
    .D(demultiplexer_1_out7), .C(clock), .Reset(reset), .Write(write), .Q(n8_bit_registry_8_q));
  _8_bit_Registry u_8_bit_registry_9 (
    .D(demultiplexer_1_out8), .C(clock), .Reset(reset), .Write(write), .Q(n8_bit_registry_9_q));
  _8_bit_Registry u_8_bit_registry_10 (
    .D(demultiplexer_1_out9), .C(clock), .Reset(reset), .Write(write), .Q(n8_bit_registry_10_q));
  _8_bit_Registry u_8_bit_registry_11 (
    .D(demultiplexer_1_out10), .C(clock), .Reset(reset), .Write(write), .Q(n8_bit_registry_11_q));
  _8_bit_Registry u_8_bit_registry_12 (
    .D(demultiplexer_1_out11), .C(clock), .Reset(reset), .Write(write), .Q(n8_bit_registry_12_q));
  _8_bit_Registry u_8_bit_registry_13 (
    .D(demultiplexer_1_out12), .C(clock), .Reset(reset), .Write(write), .Q(n8_bit_registry_13_q));
  _8_bit_Registry u_8_bit_registry_14 (
    .D(demultiplexer_1_out13), .C(clock), .Reset(reset), .Write(write), .Q(n8_bit_registry_14_q));
  _8_bit_Registry u_8_bit_registry_15 (
    .D(demultiplexer_1_out14), .C(clock), .Reset(reset), .Write(write), .Q(n8_bit_registry_15_q));
  _8_bit_Registry u_8_bit_registry_16 (
    .D(demultiplexer_1_out15), .C(clock), .Reset(reset), .Write(write), .Q(n8_bit_registry_16_q));
  Multiplexer #(.select(4), .width(8)) multiplexer_1 (
    .in0(n8_bit_registry_1_q), .in1(n8_bit_registry_2_q), .in2(n8_bit_registry_3_q),
    .in3(n8_bit_registry_4_q), .in4(n8_bit_registry_5_q), .in5(n8_bit_registry_6_q),
    .in6(n8_bit_registry_7_q), .in7(n8_bit_registry_8_q), .in8(n8_bit_registry_9_q),
    .in9(n8_bit_registry_10_q), .in10(n8_bit_registry_11_q), .in11(n8_bit_registry_12_q),
    .in12(n8_bit_registry_13_q), .in13(n8_bit_registry_14_q), .in14(n8_bit_registry_15_q),
    .in15(n8_bit_registry_16_q), .out(rs_content), .sel(rs_in));  // open: en
  Multiplexer #(.select(4), .width(8)) multiplexer_2 (
    .in0(n8_bit_registry_1_q), .in1(n8_bit_registry_2_q), .in2(n8_bit_registry_3_q),
    .in3(n8_bit_registry_4_q), .in4(n8_bit_registry_5_q), .in5(n8_bit_registry_6_q),
    .in6(n8_bit_registry_7_q), .in7(n8_bit_registry_8_q), .in8(n8_bit_registry_9_q),
    .in9(n8_bit_registry_10_q), .in10(n8_bit_registry_11_q), .in11(n8_bit_registry_12_q),
    .in12(n8_bit_registry_13_q), .in13(n8_bit_registry_14_q), .in14(n8_bit_registry_15_q),
    .in15(n8_bit_registry_16_q), .out(rt_content), .sel(rt_in));  // open: en
endmodule

module _8_bit_stack (
  input  push,
  input  pop,
  input  [7:0] data,
  input  reset,
  output out_5,
  output [7:0] out_6
);

  wire clock_1_out, comparator_1_eq, not_1_out, or_1_out, or_2_out, or_3_out;
  wire [7:0] adder_1_out, bit_extender_1_out, bit_extender_2_out, multiplexer_1_out, multiplexer_2_out,
       multiplexer_3_out, n8_bit_registry_1_q, subtractor_1_out, subtractor_2_out, subtractor_3_out;

  Clock clock_1 (.out(clock_1_out));
  assign bit_extender_1_out = {{7{1'b0}}, pop};  // Bit_Extender bit_extender_1
  Subtractor subtractor_1 (.a(n8_bit_registry_1_q), .b(bit_extender_1_out), .out(subtractor_1_out));  // open: bin, bout
  assign bit_extender_2_out = {{7{1'b0}}, push};  // Bit_Extender bit_extender_2
  or or_1 (or_1_out, push, pop);
  Adder adder_1 (.a(subtractor_1_out), .b(bit_extender_2_out), .out(adder_1_out));  // open: cin, cout
  _8_bit_Registry u_8_bit_registry_1 (
    .D(adder_1_out), .C(clock_1_out), .Reset(reset), .Write(or_1_out), .Q(n8_bit_registry_1_q));
  Subtractor subtractor_2 (.a(n8_bit_registry_1_q), .b(8'h1), .out(subtractor_2_out));  // open: bin, bout
  Subtractor subtractor_3 (.a(n8_bit_registry_1_q), .b(8'h1), .out(subtractor_3_out));  // open: bin, bout
  not not_1 (not_1_out, pop);
  Multiplexer #(.width(8)) multiplexer_1 (
    .in0(subtractor_3_out), .in1(n8_bit_registry_1_q), .out(multiplexer_1_out), .sel(not_1_out));  // open: en
  Multiplexer #(.width(8)) multiplexer_2 (
    .in0({8{1'b0}}), .in1(data), .out(multiplexer_2_out), .sel(not_1_out));  // open: en
  or or_2 (or_2_out, pop, push);
  Multiplexer #(.width(8)) multiplexer_3 (
    .in0(subtractor_2_out), .in1(multiplexer_1_out), .out(multiplexer_3_out), .sel(or_2_out));  // open: en
  or or_3 (or_3_out, pop, push);
  Comparator comparator_1 (.a({8{1'b0}}), .b(n8_bit_registry_1_q), .eq(comparator_1_eq));  // open: gt, lt
  and and_1 (out_5, comparator_1_eq, pop);
  RAM #(.bus("separate")) ram_1 (
    .addr(multiplexer_3_out), .din(multiplexer_2_out), .data(out_6), .str(or_3_out), .clk(clock_1_out),
    .ld(1'b1), .clr(reset));  // open: sel
endmodule

module Test (
  input  in_1,
  output out_2
);

  wire n;

  not not_1 (n, in_1);

  assign out_2 = in_1;
endmodule

module Register_File_2_0 (
  input  [3:0] rs_in,
  input  [3:0] rt_in,
  input  [7:0] \input ,
  input  [3:0] in_4,
  input  clock,
  input  reset,
  input  write,
  output [7:0] rs_content,
  output [7:0] rt_content
);

  wire demultiplexer_1_out0, demultiplexer_1_out1, demultiplexer_1_out2, demultiplexer_1_out3,
       demultiplexer_1_out4, demultiplexer_1_out5, demultiplexer_1_out6, demultiplexer_1_out7,
       demultiplexer_1_out8, demultiplexer_1_out9, demultiplexer_1_out10, demultiplexer_1_out11,
       demultiplexer_1_out12, demultiplexer_1_out13, demultiplexer_1_out14, demultiplexer_1_out15;
  wire [7:0] n8_bit_registry_1_q, n8_bit_registry_2_q, n8_bit_registry_3_q, n8_bit_registry_4_q,
       n8_bit_registry_5_q, n8_bit_registry_6_q, n8_bit_registry_7_q, n8_bit_registry_8_q,
       n8_bit_registry_9_q, n8_bit_registry_10_q, n8_bit_registry_11_q, n8_bit_registry_12_q,
       n8_bit_registry_13_q, n8_bit_registry_14_q, n8_bit_registry_15_q, n8_bit_registry_16_q;

  Demultiplexer #(.select(4)) demultiplexer_1 (
    .out0(demultiplexer_1_out0), .out1(demultiplexer_1_out1), .out2(demultiplexer_1_out2),
    .out3(demultiplexer_1_out3), .out4(demultiplexer_1_out4), .out5(demultiplexer_1_out5),
    .out6(demultiplexer_1_out6), .out7(demultiplexer_1_out7), .out8(demultiplexer_1_out8),
    .out9(demultiplexer_1_out9), .out10(demultiplexer_1_out10), .out11(demultiplexer_1_out11),
    .out12(demultiplexer_1_out12), .out13(demultiplexer_1_out13), .out14(demultiplexer_1_out14),
    .out15(demultiplexer_1_out15), .in(write), .sel(in_4));  // open: en
  _8_bit_Registry u_8_bit_registry_1 (
    .D(\input ), .C(clock), .Reset(reset), .Write(demultiplexer_1_out0), .Q(n8_bit_registry_1_q));
  _8_bit_Registry u_8_bit_registry_2 (
    .D(\input ), .C(clock), .Reset(reset), .Write(demultiplexer_1_out1), .Q(n8_bit_registry_2_q));
  _8_bit_Registry u_8_bit_registry_3 (
    .D(\input ), .C(clock), .Reset(reset), .Write(demultiplexer_1_out2), .Q(n8_bit_registry_3_q));
  _8_bit_Registry u_8_bit_registry_4 (
    .D(\input ), .C(clock), .Reset(reset), .Write(demultiplexer_1_out3), .Q(n8_bit_registry_4_q));
  _8_bit_Registry u_8_bit_registry_5 (
    .D(\input ), .C(clock), .Reset(reset), .Write(demultiplexer_1_out4), .Q(n8_bit_registry_5_q));
  _8_bit_Registry u_8_bit_registry_6 (
    .D(\input ), .C(clock), .Reset(reset), .Write(demultiplexer_1_out5), .Q(n8_bit_registry_6_q));
  _8_bit_Registry u_8_bit_registry_7 (
    .D(\input ), .C(clock), .Reset(reset), .Write(demultiplexer_1_out6), .Q(n8_bit_registry_7_q));
  _8_bit_Registry u_8_bit_registry_8 (
    .D(\input ), .C(clock), .Reset(reset), .Write(demultiplexer_1_out7), .Q(n8_bit_registry_8_q));
  _8_bit_Registry u_8_bit_registry_9 (
    .D(\input ), .C(clock), .Reset(reset), .Write(demultiplexer_1_out8), .Q(n8_bit_registry_9_q));
  _8_bit_Registry u_8_bit_registry_10 (
    .D(\input ), .C(clock), .Reset(reset), .Write(demultiplexer_1_out9), .Q(n8_bit_registry_10_q));
  _8_bit_Registry u_8_bit_registry_11 (
    .D(\input ), .C(clock), .Reset(reset), .Write(demultiplexer_1_out10), .Q(n8_bit_registry_11_q));
  _8_bit_Registry u_8_bit_registry_12 (
    .D(\input ), .C(clock), .Reset(reset), .Write(demultiplexer_1_out11), .Q(n8_bit_registry_12_q));
  _8_bit_Registry u_8_bit_registry_13 (
    .D(\input ), .C(clock), .Reset(reset), .Write(demultiplexer_1_out12), .Q(n8_bit_registry_13_q));
  _8_bit_Registry u_8_bit_registry_14 (
    .D(\input ), .C(clock), .Reset(reset), .Write(demultiplexer_1_out13), .Q(n8_bit_registry_14_q));
  _8_bit_Registry u_8_bit_registry_15 (
    .D(\input ), .C(clock), .Reset(reset), .Write(demultiplexer_1_out14), .Q(n8_bit_registry_15_q));
  _8_bit_Registry u_8_bit_registry_16 (
    .D(\input ), .C(clock), .Reset(reset), .Write(demultiplexer_1_out15), .Q(n8_bit_registry_16_q));
  Multiplexer #(.select(4), .width(8)) multiplexer_1 (
    .in0(n8_bit_registry_1_q), .in1(n8_bit_registry_2_q), .in2(n8_bit_registry_3_q),
    .in3(n8_bit_registry_4_q), .in4(n8_bit_registry_5_q), .in5(n8_bit_registry_6_q),
    .in6(n8_bit_registry_7_q), .in7(n8_bit_registry_8_q), .in8(n8_bit_registry_9_q),
    .in9(n8_bit_registry_10_q), .in10(n8_bit_registry_11_q), .in11(n8_bit_registry_12_q),
    .in12(n8_bit_registry_13_q), .in13(n8_bit_registry_14_q), .in14(n8_bit_registry_15_q),
    .in15(n8_bit_registry_16_q), .out(rs_content), .sel(rs_in));  // open: en
  Multiplexer #(.select(4), .width(8)) multiplexer_2 (
    .in0(n8_bit_registry_1_q), .in1(n8_bit_registry_2_q), .in2(n8_bit_registry_3_q),
    .in3(n8_bit_registry_4_q), .in4(n8_bit_registry_5_q), .in5(n8_bit_registry_6_q),
    .in6(n8_bit_registry_7_q), .in7(n8_bit_registry_8_q), .in8(n8_bit_registry_9_q),
    .in9(n8_bit_registry_10_q), .in10(n8_bit_registry_11_q), .in11(n8_bit_registry_12_q),
    .in12(n8_bit_registry_13_q), .in13(n8_bit_registry_14_q), .in14(n8_bit_registry_15_q),
    .in15(n8_bit_registry_16_q), .out(rt_content), .sel(rt_in));  // open: en
endmodule
