// Logisim project SD_Group50.circ as structural Verilog: 5 circuits, main circuit main
module main (
  output [7:0] pc,
  output [7:0] r0,
  output [7:0] r1,
  output [7:0] r2,
  output [7:0] r3,
  output [7:0] r4,
  output [7:0] r5,
  output [7:0] r6,
  output [7:0] r7,
  output [7:0] r8,
  output [7:0] r9,
  output [7:0] r10,
  output [7:0] r11,
  output [7:0] r12,
  output [7:0] r13,
  output [7:0] r14,
  output [7:0] r15,
  output halt
);

  wire and_1_out, clock_1_out, datapath_1_c, datapath_1_clr, datapath_1_ld, datapath_1_str, reset_out;
  wire [7:0] datapath_1_a, datapath_1_d, ram_2_data;
  wire [15:0] ram_1_data;

  Halt halt_1 (.instruction(ram_1_data), .clock(clock_1_out), .reset(reset_out), .halt(halt));
  Clock clock_1 (.out(clock_1_out));
  Button reset (.out(reset_out));
  and and_1 (and_1_out, ~halt, clock_1_out);  // AND_Gate
  _8_bit_PC u_8_bit_pc_1 (
    .Branch_relative(1'b0), .Branch_absolute(1'b0), .Branch_value({8{1'b0}}), .C(and_1_out),
    .Reset(reset_out), .Adress_in_instruction_memory(pc));
  RAM #(.dataWidth(16)) ram_1 (.addr(pc), .data(ram_1_data), .ld(1'b1), .clr(reset_out));  // open: sel, clk
  Datapath datapath_1 (
    .Instruction(ram_1_data), .Clock(and_1_out), .Reset(reset_out), .out_11(r15), .out_13(r14), .out_14(r13),
    .out_15(r12), .out_16(r11), .out_17(r10), .out_18(r9), .out_19(r8), .out_20(r7), .out_21(r6),
    .out_22(r5), .out_23(r4), .out_24(r3), .out_25(r2), .out_26(r1), .out_27(r0), .A(datapath_1_a),
    .D(datapath_1_d), .str(datapath_1_str), .C(datapath_1_c), .ld(datapath_1_ld), .clr(datapath_1_clr),
    .D_read(ram_2_data));  // open: Overflow
  RAM #(.bus("separate")) ram_2 (
    .addr(datapath_1_a), .din(datapath_1_d), .data(ram_2_data), .str(datapath_1_str), .clk(datapath_1_c),
    .ld(datapath_1_ld), .clr(datapath_1_clr));  // open: sel

  // Notes on the sheet:
  //   current instruction
  //   clock signal
  //   reset button
  //   DO NOT CHANGE THE INPUTS AND OUTPUTS OF THIS CIRCUIT! Do not add/remove inputs or outputs. Do not even change their location or orientation.
endmodule

module Halt (
  input  [15:0] instruction,
  input  clock,
  input  reset,
  output halt
);

  wire and_1_out, comparator_1_eq, comparator_2_gt, counter_1_carry, or_1_out, or_2_out;
  wire [11:0] counter_1_q;

  Comparator #(.width(16), .mode("unsigned")) comparator_1 (
    .a(instruction), .b({16{1'b0}}), .eq(comparator_1_eq));  // open: gt, lt
  Counter #(.width(12), .max('hfff), .trigger("falling")) counter_1 (
    .Q(counter_1_q), .carry(counter_1_carry), .clk(clock), .clr(reset));  // open: load, D, count
  or or_1 (or_1_out, comparator_1_eq, counter_1_carry);
  Comparator #(.width(12), .mode("unsigned")) comparator_2 (
    .a(counter_1_q), .b({12{1'b0}}), .gt(comparator_2_gt));  // open: eq, lt
  or or_2 (or_2_out, halt, and_1_out);
  and and_1 (and_1_out, or_1_out, comparator_2_gt);
  Register #(.width(1)) register_1 (.D(or_2_out), .Q(halt), .clk(clock), .clr(reset));  // open: en

  // Notes on the sheet:
  //   halt becomes and stays asserted if the instruction is 0000 (not in the first clock cycle) or the end of the counter is reached (2^12)
endmodule

module _8_bit_PC (
  input  Branch_relative,
  input  Branch_absolute,
  input  [7:0] Branch_value,
  input  C,
  input  Reset,
  output [7:0] Adress_in_instruction_memory
);

  wire and_1_out, and_2_out, and_3_out, not_1_out, not_2_out, not_3_out, not_4_out;
  wire [7:0] adder_1_out, adder_2_out, and_4_out, and_5_out, and_6_out, bit_extender_1_out,
       bit_extender_2_out, bit_extender_3_out, or_1_out;

  Adder adder_1 (.a(Adress_in_instruction_memory), .b(8'h1), .out(adder_1_out));  // open: cin, cout
  Adder adder_2 (.a(Adress_in_instruction_memory), .b(Branch_value), .out(adder_2_out));  // open: cin, cout
  not not_1 (not_1_out, Branch_relative);
  not not_2 (not_2_out, Branch_absolute);
  not not_3 (not_3_out, Branch_absolute);
  not not_4 (not_4_out, Branch_relative);
  and and_1 (and_1_out, not_1_out, not_2_out);
  and and_2 (and_2_out, Branch_relative, not_3_out);
  and and_3 (and_3_out, not_4_out, Branch_absolute);
  assign bit_extender_1_out = {{7{and_1_out}}, and_1_out};  // Bit_Extender bit_extender_1
  assign bit_extender_2_out = {{7{and_2_out}}, and_2_out};  // Bit_Extender bit_extender_2
  assign bit_extender_3_out = {{7{and_3_out}}, and_3_out};  // Bit_Extender bit_extender_3
  assign and_4_out = bit_extender_1_out & adder_1_out;  // AND_Gate and_4, 8 bits wide
  assign and_5_out = bit_extender_2_out & adder_2_out;  // AND_Gate and_5, 8 bits wide
  assign and_6_out = bit_extender_3_out & Branch_value;  // AND_Gate and_6, 8 bits wide
  assign or_1_out = and_6_out | and_5_out | and_4_out;  // OR_Gate or_1, 8 bits wide
  _8_bit_Registry Register__containing_current_adress (
    .D(or_1_out), .C(C), .Reset(Reset), .Write(C), .Q(Adress_in_instruction_memory));

  // Notes on the sheet:
  //   CALCULATING THE NEXT ADRESS
  //   Default: +1 each cycle
  //   Branch relative: +Branch value
  //   Branch absolute: = Branch value
  //   Instruction can only change once per clock cycle, so only write once per clock cycle
  //   DECIDING THE NEXT ADRESS
  //   Default: Not relative, not absolute
  //   Branch relative: Relative, not absolute
  //   Branch absolute: Not relative, absolute
endmodule

module blub (
  input  [15:0] Instruction,
  output overflow
);

  wire clock_out, reset_button_out;
  wire [3:0] demultiplexer_1_out0, demultiplexer_1_out2, demultiplexer_1_out3, demultiplexer_1_out4,
       demultiplexer_1_out5, demultiplexer_1_out6, demultiplexer_1_out7, demultiplexer_1_out8,
       demultiplexer_1_out9, demultiplexer_1_out10, demultiplexer_1_out11, demultiplexer_1_out12,
       demultiplexer_1_out13, multiplexer_1_out;
  wire [7:0] n8_bit_alu_1_result, ram_1_data, register_file_1_rs_content, register_file_1_rt_content;

  Clock clock (.out(clock_out));
  Button reset_button (.out(reset_button_out));
  Demultiplexer #(.select(4), .width(4)) demultiplexer_1 (
    .out0(demultiplexer_1_out0), .out2(demultiplexer_1_out2), .out3(demultiplexer_1_out3),
    .out4(demultiplexer_1_out4), .out5(demultiplexer_1_out5), .out6(demultiplexer_1_out6),
    .out7(demultiplexer_1_out7), .out8(demultiplexer_1_out8), .out9(demultiplexer_1_out9),
    .out10(demultiplexer_1_out10), .out11(demultiplexer_1_out11), .out12(demultiplexer_1_out12),
    .out13(demultiplexer_1_out13), .in(Instruction[15:12]), .sel(Instruction[15:12]));  // open: out1, out14, out15, en
  Multiplexer #(.select(4), .width(4)) multiplexer_1 (
    .in0(demultiplexer_1_out0), .in1(Instruction[7:4]), .in2(demultiplexer_1_out2),
    .in3(demultiplexer_1_out3), .in4(demultiplexer_1_out4), .in5(demultiplexer_1_out5),
    .in6(demultiplexer_1_out6), .in7(demultiplexer_1_out7), .in8(demultiplexer_1_out8),
    .in9(demultiplexer_1_out9), .in10(demultiplexer_1_out10), .in11(demultiplexer_1_out11),
    .in12(demultiplexer_1_out12), .in13(demultiplexer_1_out13), .out(multiplexer_1_out),
    .sel(Instruction[15:12]));  // open: in14, in15, en
  RAM #(.addrWidth(4), .bus("separate")) ram_1 (
    .addr(Instruction[11:8]), .data(ram_1_data));  // open: din, str, sel, clk, ld, clr
  Register_file register_file_1 (
    .rs_in(Instruction[7:4]), .rt_in(Instruction[3:0]), .\input (n8_bit_alu_1_result),
    .in_4(Instruction[11:8]), .clock(clock_out), .reset(reset_button_out), .write(1'b1),
    .rs_content(register_file_1_rs_content), .rt_content(register_file_1_rt_content));
  _8_bit_ALU u_8_bit_alu_1 (
    .ALU_code(multiplexer_1_out), .a(register_file_1_rs_content), .b(register_file_1_rt_content),
    .result(n8_bit_alu_1_result), .overflow(overflow));

  // Notes on the sheet:
  //   op
  //   rs
  //   rd
  //   rt
  //   maar ik heb geen flauw idee hoe dat moet werken
  //   de test file van 3 zal dat wel snel uitwijzen ;)
  //   voor de sb en lb moet er nog een ram module zijn om op te slagen en te laden
  //   alles van bewerkingen die opgeslagen worden in het register zouden moeten werken
  //   sb en lb
  //   hier moet nog iets komen voor lb en sb
  //   dit is eig om ervoor te zorgen dat wnr op = 0001 dat rt gebruikt wordt als op
  //   ops door rt uitgevoerd
  //   register
  //   uitkomst wordt opgeslagen in rd
endmodule

module Datapath (
  input  [15:0] Instruction,
  input  Clock,
  input  Reset,
  input  [7:0] D_read,
  output [7:0] A,
  output [7:0] D,
  output str,
  output C,
  output ld,
  output clr,
  output [7:0] out_11,
  output Overflow,
  output [7:0] out_13,
  output [7:0] out_14,
  output [7:0] out_15,
  output [7:0] out_16,
  output [7:0] out_17,
  output [7:0] out_18,
  output [7:0] out_19,
  output [7:0] out_20,
  output [7:0] out_21,
  output [7:0] out_22,
  output [7:0] out_23,
  output [7:0] out_24,
  output [7:0] out_25,
  output [7:0] out_26,
  output [7:0] out_27
);

  wire comparator_3_eq, imm_out, not_1_out, or_1_out, write_out;
  wire [3:0] _0001_out, _1010_out, _1011_out, bit_extender_1_out, bit_extender_2_out, bit_extender_3_out,
       bit_extender_4_out, Else_out, multiplexer_1_out, or_2_out;
  wire [7:0] bit_extender_5_out, bit_extender_6_out, multiplexer_2_out, multiplexer_3_out, multiplexer_4_out,
       Register_file_rs_content;

  or write (write_out, not_1_out, comparator_3_eq, ld);
  Multiplexer #(.width(4)) multiplexer_1 (
    .in0(Instruction[3:0]), .in1(Instruction[11:8]), .out(multiplexer_1_out), .sel(imm_out));  // open: en
  Multiplexer #(.width(8)) multiplexer_2 (.in0(A), .in1(D_read), .out(multiplexer_2_out), .sel(ld));  // open: en
  or or_1 (or_1_out, comparator_3_eq, ld, str);
  not not_1 (not_1_out, or_1_out);
  Comparator #(.width(4)) comparator_1 (.a(4'b1011), .b(Instruction[15:12]), .eq(str));  // open: gt, lt
  Comparator #(.width(4)) comparator_2 (.a(4'b1010), .b(Instruction[15:12]), .eq(ld));  // open: gt, lt
  Comparator #(.width(4)) comparator_3 (.a(4'b0001), .b(Instruction[15:12]), .eq(comparator_3_eq));  // open: gt, lt
  assign bit_extender_1_out = {{3{not_1_out}}, not_1_out};  // Bit_Extender bit_extender_1
  assign bit_extender_2_out = {{3{str}}, str};  // Bit_Extender bit_extender_2
  assign bit_extender_3_out = {{3{ld}}, ld};  // Bit_Extender bit_extender_3
  assign bit_extender_4_out = {{3{comparator_3_eq}}, comparator_3_eq};  // Bit_Extender bit_extender_4
  assign Else_out = Instruction[15:12] & bit_extender_1_out;  // AND_Gate Else, 4 bits wide
  assign _1011_out = bit_extender_2_out & 4'b0100;  // AND_Gate _1011, 4 bits wide
  assign _1010_out = bit_extender_3_out & 4'b0100;  // AND_Gate _1010, 4 bits wide
  assign _0001_out = bit_extender_4_out & Instruction[3:0];  // AND_Gate _0001, 4 bits wide
  assign or_2_out = _0001_out | _1010_out | _1011_out | Else_out;  // OR_Gate or_2, 4 bits wide
  Register_File_2_0 Register_file (
    .rs_in(Instruction[7:4]), .rt_in(multiplexer_1_out), .\input (multiplexer_2_out),
    .in_4(Instruction[11:8]), .clock(Clock), .reset(Reset), .write(write_out), .out_10(out_11),
    .out_11(out_13), .out_12(out_14), .out_13(out_15), .out_14(out_16), .out_15(out_17), .out_16(out_18),
    .out_17(out_19), .out_18(out_20), .out_19(out_21), .out_20(out_22), .out_21(out_23), .out_22(out_24),
    .out_23(out_25), .out_24(out_26), .out_25(out_27), .rs_content(Register_file_rs_content), .rt_content(D));
  assign bit_extender_5_out = {{4{1'b0}}, Instruction[7:4]};  // Bit_Extender bit_extender_5
  assign bit_extender_6_out = {{4{1'b0}}, Instruction[3:0]};  // Bit_Extender bit_extender_6
  Multiplexer #(.width(8)) multiplexer_3 (
    .in0(Register_file_rs_content), .in1(bit_extender_5_out), .out(multiplexer_3_out), .sel(imm_out));  // open: en
  or imm (imm_out, ld, str);
  Multiplexer #(.width(8)) multiplexer_4 (
    .in0(D), .in1(bit_extender_6_out), .out(multiplexer_4_out), .sel(imm_out));  // open: en
  _8_bit_ALU u_8_bit_alu_1 (
    .ALU_code(or_2_out), .a(multiplexer_3_out), .b(multiplexer_4_out), .result(A), .overflow(Overflow));

  assign C = Clock;
  assign clr = Reset;

  // Notes on the sheet:
  //   op
  //   rs
  //   rd
  //   rt
  //   rs en rt
  //   Else -> use op as op code
  //   op add
  //   Opcode == 0001 -> use rt as op code
  //   Opcode == 1010 -> lb at position (rs+rt) to rd
  //   Opcode == 1011 -> sb at position rd to (rs+rt) 
  //   rt
  //   Resultaat vd ALU
  //   lb
  //   adress + offset
  //   rt
  //   gelezen lb
endmodule
