// Logisim project Control Unit.circ as structural Verilog: 1 circuit, main circuit Control Unit
module Control_Unit (
  input  [3:0] opcode,
  input  [3:0] rt,
  output Double_ALU,
  output Single_ALU,
  output lb,
  output sb,
  output ldi,
  output addi,
  output beq,
  output blt,
  output jal,
  output j,
  output jr,
  output Write_reg,
  output read_rd_from_reg_instead_of_rt,
  output ALU_b__immidiate_instead_of_rt,
  output [3:0] Opcode_2
);

  wire comparator_1_eq, comparator_8_eq, comparator_9_eq, comparator_10_eq, not_2_out, or_1_out, or_2_out,
       or_3_out;
  wire [3:0] and_5_out, and_6_out, and_7_out, and_8_out, and_9_out, bit_extender_1_out, bit_extender_2_out,
       bit_extender_3_out, bit_extender_4_out, bit_extender_5_out;

  not not_1 (Double_ALU, or_1_out);
  or or_1 (or_1_out, comparator_1_eq, lb, read_rd_from_reg_instead_of_rt, ldi, addi, beq, blt);
  Comparator #(.width(4)) comparator_1 (.a(4'b0001), .b(opcode), .eq(comparator_1_eq));  // open: gt, lt
  Comparator #(.width(4)) comparator_2 (.a(4'b1010), .b(opcode), .eq(lb));  // open: gt, lt
  Comparator #(.width(4)) comparator_3 (.a(4'b1011), .b(opcode), .eq(read_rd_from_reg_instead_of_rt));  // open: gt, lt
  Comparator #(.width(4)) comparator_4 (.a(4'b1100), .b(opcode), .eq(ldi));  // open: gt, lt
  Comparator #(.width(4)) comparator_5 (.a(4'b1101), .b(opcode), .eq(addi));  // open: gt, lt
  Comparator #(.width(4)) comparator_6 (.a(4'b1110), .b(opcode), .eq(beq));  // open: gt, lt
  Comparator #(.width(4)) comparator_7 (.a(4'b1111), .b(opcode), .eq(blt));  // open: gt, lt
  and and_1 (Single_ALU, not_2_out, comparator_1_eq);
  not not_2 (not_2_out, or_2_out);
  or or_2 (or_2_out, comparator_8_eq, comparator_9_eq, comparator_10_eq);
  Comparator #(.width(4)) comparator_8 (.a(4'b0100), .b(rt), .eq(comparator_8_eq));  // open: gt, lt
  Comparator #(.width(4)) comparator_9 (.a(4'b0011), .b(rt), .eq(comparator_9_eq));  // open: gt, lt
  Comparator #(.width(4)) comparator_10 (.a(4'b0010), .b(rt), .eq(comparator_10_eq));  // open: gt, lt
  and and_2 (jal, comparator_8_eq, comparator_1_eq);
  and and_3 (j, comparator_9_eq, comparator_1_eq);
  and and_4 (jr, comparator_10_eq, comparator_1_eq);
  or or_3 (or_3_out, lb, read_rd_from_reg_instead_of_rt, addi);
  assign bit_extender_1_out = {{3{Double_ALU}}, Double_ALU};  // Bit_Extender bit_extender_1
  assign and_5_out = bit_extender_1_out & opcode;  // AND_Gate and_5, 4 bits wide
  assign bit_extender_2_out = {{3{Single_ALU}}, Single_ALU};  // Bit_Extender bit_extender_2
  assign and_6_out = bit_extender_2_out & rt;  // AND_Gate and_6, 4 bits wide
  assign bit_extender_3_out = {{3{or_3_out}}, or_3_out};  // Bit_Extender bit_extender_3
  assign and_7_out = bit_extender_3_out & 4'b0100;  // AND_Gate and_7, 4 bits wide
  assign bit_extender_4_out = {{3{beq}}, beq};  // Bit_Extender bit_extender_4
  assign and_8_out = bit_extender_4_out & 4'b1000;  // AND_Gate and_8, 4 bits wide
  assign bit_extender_5_out = {{3{blt}}, blt};  // Bit_Extender bit_extender_5
  or or_4 (Write_reg, Double_ALU, Single_ALU, lb, ldi, addi, jal);
  or or_5 (ALU_b__immidiate_instead_of_rt, lb, read_rd_from_reg_instead_of_rt, addi);
  assign and_9_out = bit_extender_5_out & 4'b0110;  // AND_Gate and_9, 4 bits wide
  assign Opcode_2 = and_5_out | and_6_out | and_7_out | and_8_out | and_9_out;  // OR_Gate or_6, 4 bits wide

  assign sb = read_rd_from_reg_instead_of_rt;

  // Notes on the sheet:
  //   Geen enkele van de onderstaande:
  //   Single ALU:
  //   lb:
  //   sb:
  //   ldi:
  //   addi:
  //   beq:
  //   blt:
  //   = Double ALU
  //   Opcode == 0001 -> use rt as op code
  //   Opcode == 1010 -> lb at position (rs+rt) to rd
  //   jal
  //   j
  //   jr
  //   Double ALU
  //   Single ALU
  //   ALU add: lb, sb, addi
endmodule
