// Logisim project SD_Group50.circ as structural Verilog: 8 circuits, main circuit main
module main (
  output [7:0] pc,
  output [7:0] r0,
  output [7:0] r1,
  output [7:0] r2,
  output [7:0] r3,
  output [7:0] r4,
  output [7:0] r5,
  output [7:0] r6,
  output [7:0] r7,
  output [7:0] r8,
  output [7:0] r9,
  output [7:0] r10,
  output [7:0] r11,
  output [7:0] r15,
  output halt
);

  wire and_1_out, and_2_out, clock_1_out, control_unit_1_absolute_instr, control_unit_1_addi,
       control_unit_1_beq, control_unit_1_blt, control_unit_1_error__unknown_instruction, control_unit_1_j,
       control_unit_1_jal, control_unit_1_jr, control_unit_1_lb, control_unit_1_ldi,
       control_unit_1_read_rd_from_reg_instead_of_rt__todo__remove, control_unit_1_reg_output_2_to_alu_a,
       control_unit_1_rel_instr_possible, control_unit_1_sb, control_unit_1_write_reg, n8_bit_alu_1_overflow,
       or_1_out, reset_out;
  wire [0:0] n8_bit_alu_1_result;
  wire [1:0] control_unit_1_alu_b__rt00_imm01_s10, control_unit_1_register_store_alub00_data01_rs10;
  wire [3:0] control_unit_1_opcode, control_unit_1_rd, control_unit_1_rs, control_unit_1_rt,
       multiplexer_2_out, multiplexer_3_out;
  wire [6:0] n8_bit_alu_1_result_2;
  wire [7:0] adder_1_out, immidiate_unit_1_out_13, multiplexer_1_out, multiplexer_4_out, multiplexer_5_out,
       multiplexer_6_out, r12, r13, r14, ram_2_data, Register_file_rs_content, Register_file_rt_content;
  wire [15:0] ram_1_data;

  Halt halt_1 (.instruction(ram_1_data), .clock(clock_1_out), .reset(reset_out), .in_2(or_1_out), .halt(halt));
  Clock clock_1 (.out(clock_1_out));
  Button reset (.out(reset_out));
  Multiplexer #(.width(8)) multiplexer_1 (
    .in0(immidiate_unit_1_out_13), .in1({n8_bit_alu_1_result_2, n8_bit_alu_1_result[0]}),
    .out(multiplexer_1_out), .sel(control_unit_1_jr));  // open: en
  and and_1 (and_1_out, ~halt, clock_1_out);  // AND_Gate
  or or_1 (or_1_out, control_unit_1_error__unknown_instruction, n8_bit_alu_1_overflow);
  _8_bit_PC u_8_bit_pc_1 (
    .Branch_relative(and_2_out), .Branch_absolute(control_unit_1_absolute_instr),
    .Branch_value(multiplexer_1_out), .C(and_1_out), .Reset(reset_out), .Adress_in_instruction_memory(pc));
  Adder adder_1 (.a(pc), .b(8'h1), .out(adder_1_out));  // open: cin, cout
  and and_2 (and_2_out, n8_bit_alu_1_result[0], control_unit_1_rel_instr_possible);
  RAM #(.dataWidth(16)) ram_1 (.addr(pc), .data(ram_1_data), .ld(1'b1), .clr(reset_out));  // open: sel, clk
  Control_Unit control_unit_1 (
    .in_1(ram_1_data), .rd(control_unit_1_rd), .rs(control_unit_1_rs), .rt(control_unit_1_rt),
    .ERROR__Unknown_Instruction(control_unit_1_error__unknown_instruction), .lb(control_unit_1_lb),
    .sb(control_unit_1_sb), .ldi(control_unit_1_ldi), .addi(control_unit_1_addi), .beq(control_unit_1_beq),
    .blt(control_unit_1_blt), .jal(control_unit_1_jal), .j(control_unit_1_j), .jr(control_unit_1_jr),
    .Write_reg(control_unit_1_write_reg),
    .read_rd_from_reg_instead_of_rt__TODO__Remove(control_unit_1_read_rd_from_reg_instead_of_rt__todo__remove),
    .ALU_b__rt00_imm01_s10(control_unit_1_alu_b__rt00_imm01_s10),
    .register_store_ALUb00_DATA01_rs10(control_unit_1_register_store_alub00_data01_rs10),
    .absolute_instr(control_unit_1_absolute_instr), .rel_instr_possible(control_unit_1_rel_instr_possible),
    .reg_output_2_to_alu_a(control_unit_1_reg_output_2_to_alu_a), .Opcode(control_unit_1_opcode));  // open: opcode_2, Double_ALU, Single_ALU
  Multiplexer #(.width(4)) multiplexer_2 (
    .in0(control_unit_1_rd), .in1(4'b1111), .out(multiplexer_2_out), .sel(control_unit_1_jal));  // open: en
  Multiplexer #(.width(4)) multiplexer_3 (
    .in0(control_unit_1_rt), .in1(control_unit_1_rd), .out(multiplexer_3_out),
    .sel(control_unit_1_read_rd_from_reg_instead_of_rt__todo__remove));  // open: en
  Multiplexer #(.select(2), .width(8)) multiplexer_4 (
    .in0({n8_bit_alu_1_result_2, n8_bit_alu_1_result[0]}), .in1(ram_2_data), .in2(adder_1_out),
    .in3({control_unit_1_rs, control_unit_1_rt}), .out(multiplexer_4_out),
    .sel(control_unit_1_register_store_alub00_data01_rs10));  // open: en
  Register_File_2_0 Register_file (
    .rs_in(control_unit_1_rs), .rt_in(multiplexer_3_out), .\input (multiplexer_4_out),
    .in_4(multiplexer_2_out), .clock(and_1_out), .reset(reset_out), .write(control_unit_1_write_reg),
    .out_10(r15), .out_11(r14), .out_12(r13), .out_13(r12), .out_14(r11), .out_15(r10), .out_16(r9),
    .out_17(r8), .out_18(r7), .out_19(r6), .out_20(r5), .out_21(r4), .out_22(r3), .out_23(r2), .out_24(r1),
    .out_25(r0), .rs_content(Register_file_rs_content), .rt_content(Register_file_rt_content));
  immidiate_unit immidiate_unit_1 (
    .rs(control_unit_1_rs), .rt(control_unit_1_rt), .ldi(control_unit_1_ldi), .lb(control_unit_1_lb),
    .sb(control_unit_1_sb), .addi(control_unit_1_addi), .beq(control_unit_1_beq), .blt(control_unit_1_blt),
    .out_13(immidiate_unit_1_out_13), .jr(control_unit_1_jr), .rd(control_unit_1_rd), .j(control_unit_1_j),
    .jal(control_unit_1_jal));
  Multiplexer #(.width(8)) multiplexer_5 (
    .in0(Register_file_rs_content), .in1(Register_file_rt_content), .out(multiplexer_5_out),
    .sel(control_unit_1_reg_output_2_to_alu_a));  // open: en
  Multiplexer #(.select(2), .width(8)) multiplexer_6 (
    .in0(Register_file_rt_content), .in1(immidiate_unit_1_out_13), .in2(Register_file_rs_content),
    .out(multiplexer_6_out), .sel(control_unit_1_alu_b__rt00_imm01_s10));  // open: in3, en
  _8_bit_ALU u_8_bit_alu_1 (
    .ALU_code(control_unit_1_opcode), .a(multiplexer_5_out), .b(multiplexer_6_out),
    .result({n8_bit_alu_1_result_2, n8_bit_alu_1_result[0]}), .overflow(n8_bit_alu_1_overflow));
  RAM #(.bus("separate")) ram_2 (
    .addr({n8_bit_alu_1_result_2, n8_bit_alu_1_result[0]}), .din(Register_file_rt_content),
    .data(ram_2_data), .str(control_unit_1_sb), .clk(and_1_out), .ld(control_unit_1_lb), .clr(reset_out));  // open: sel

  // Notes on the sheet:
  //   current instruction
  //   clock signal
  //   reset button
  //   TODO: jr springt naar $rd + imm ipv imm
  //   DO NOT CHANGE THE INPUTS AND OUTPUTS OF THIS CIRCUIT! Do not add/remove inputs or outputs. Do not even change their location or orientation.
  //   Input immidiate unit
  //   TODO: signed imm in rs extenden
  //   Extend unsigned = 0'en toevoegen
  //   Resultaat immidiate unit (incl keuze rs/rt)
endmodule

module Halt (
  input  [15:0] instruction,
  input  in_2,
  input  clock,
  input  reset,
  output halt
);

  wire and_1_out, comparator_1_eq, comparator_2_gt, counter_1_carry, or_1_out, or_2_out, register_1_q;
  wire [11:0] counter_1_q;

  Comparator #(.width(16), .mode("unsigned")) comparator_1 (
    .a(instruction), .b({16{1'b0}}), .eq(comparator_1_eq));  // open: gt, lt
  Counter #(.width(12), .max('hfff), .trigger("falling")) counter_1 (
    .Q(counter_1_q), .carry(counter_1_carry), .clk(clock), .clr(reset));  // open: load, D, count
  or or_1 (or_1_out, comparator_1_eq, counter_1_carry);
  Comparator #(.width(12), .mode("unsigned")) comparator_2 (
    .a(counter_1_q), .b({12{1'b0}}), .gt(comparator_2_gt));  // open: eq, lt
  or or_2 (or_2_out, register_1_q, and_1_out);
  and and_1 (and_1_out, or_1_out, comparator_2_gt);
  Register #(.width(1)) register_1 (.D(or_2_out), .Q(register_1_q), .clk(clock), .clr(reset));  // open: en
  or or_3 (halt, register_1_q, in_2);

  // Notes on the sheet:
  //   halt becomes and stays asserted if the instruction is 0000 (not in the first clock cycle) or the end of the counter is reached (2^12)
endmodule

module _8_bit_PC (
  input  Branch_relative,
  input  Branch_absolute,
  input  [7:0] Branch_value,
  input  C,
  input  Reset,
  output [7:0] Adress_in_instruction_memory
);

  wire and_1_out, and_2_out, and_3_out, not_1_out, not_2_out, not_3_out, not_4_out;
  wire [7:0] adder_1_out, adder_2_out, adder_3_out, and_4_out, and_5_out, and_6_out, bit_extender_1_out,
       bit_extender_2_out, bit_extender_3_out, or_1_out;

  Adder adder_1 (.a(Adress_in_instruction_memory), .b(8'h1), .out(adder_1_out));  // open: cin, cout
  Adder adder_2 (.a(Adress_in_instruction_memory), .b(Branch_value), .out(adder_2_out));  // open: cin, cout
  Adder adder_3 (.a(adder_2_out), .b(8'h1), .out(adder_3_out));  // open: cin, cout
  not not_1 (not_1_out, Branch_relative);
  not not_2 (not_2_out, Branch_absolute);
  not not_3 (not_3_out, Branch_absolute);
  not not_4 (not_4_out, Branch_relative);
  and and_1 (and_1_out, not_1_out, not_2_out);
  and and_2 (and_2_out, Branch_relative, not_3_out);
  and and_3 (and_3_out, not_4_out, Branch_absolute);
  assign bit_extender_1_out = {{7{and_1_out}}, and_1_out};  // Bit_Extender bit_extender_1
  assign bit_extender_2_out = {{7{and_2_out}}, and_2_out};  // Bit_Extender bit_extender_2
  assign bit_extender_3_out = {{7{and_3_out}}, and_3_out};  // Bit_Extender bit_extender_3
  assign and_4_out = bit_extender_1_out & adder_1_out;  // AND_Gate and_4, 8 bits wide
  assign and_5_out = bit_extender_2_out & adder_3_out;  // AND_Gate and_5, 8 bits wide
  assign and_6_out = bit_extender_3_out & Branch_value;  // AND_Gate and_6, 8 bits wide
  assign or_1_out = and_6_out | and_5_out | and_4_out;  // OR_Gate or_1, 8 bits wide
  _8_bit_Registry Register__containing_current_adress (
    .D(or_1_out), .C(C), .Reset(Reset), .Write(1'b1), .Q(Adress_in_instruction_memory));

  // Notes on the sheet:
  //   CALCULATING THE NEXT ADRESS
  //   Default: +1 each cycle
  //   TODO: Check if +1 is needed
  //   Branch relative: +Branch value
  //   Branch absolute: = Branch value
  //   Instruction can only change once per clock cycle, so only write once per clock cycle
  //   DECIDING THE NEXT ADRESS
  //   Default: Not relative, not absolute
  //   Branch relative: Relative, not absolute
  //   Branch absolute: Not relative, absolute
endmodule

module Datapath (
  input  [15:0] Instruction,
  input  Clock,
  input  Reset,
  input  [7:0] D_read,
  output [7:0] A,
  output [7:0] D,
  output str,
  output C,
  output ld,
  output clr,
  output [7:0] out_11,
  output Overflow,
  output [7:0] out_13,
  output [7:0] out_14,
  output [7:0] out_15,
  output [7:0] out_16,
  output [7:0] out_17,
  output [7:0] out_18,
  output [7:0] out_19,
  output [7:0] out_20,
  output [7:0] out_21,
  output [7:0] out_22,
  output [7:0] out_23,
  output [7:0] out_24,
  output [7:0] out_25,
  output [7:0] out_26,
  output [7:0] out_27
);

  wire comparator_3_eq, imm_out, not_1_out, or_1_out, write_out;
  wire [3:0] _0001_out, _1010_out, _1011_out, bit_extender_1_out, bit_extender_2_out, bit_extender_3_out,
       bit_extender_4_out, Else_out, multiplexer_1_out, or_2_out;
  wire [7:0] bit_extender_5_out, multiplexer_2_out, multiplexer_3_out, Register_file_rs_content;

  // equal equal_1: pin names not known; wires that end beside it: Clock
  or write (write_out, not_1_out, comparator_3_eq, ld);
  Multiplexer #(.width(4)) multiplexer_1 (
    .in0(Instruction[3:0]), .in1(Instruction[11:8]), .out(multiplexer_1_out), .sel(imm_out));  // open: en
  Multiplexer #(.width(8)) multiplexer_2 (.in0(A), .in1(D_read), .out(multiplexer_2_out), .sel(ld));  // open: en
  not not_1 (not_1_out, or_1_out);
  or or_1 (or_1_out, comparator_3_eq, ld, str);
  Comparator #(.width(4)) comparator_1 (.a(4'b1011), .b(Instruction[15:12]), .eq(str));  // open: gt, lt
  Comparator #(.width(4)) comparator_2 (.a(4'b1010), .b(Instruction[15:12]), .eq(ld));  // open: gt, lt
  Comparator #(.width(4)) comparator_3 (.a(4'b0001), .b(Instruction[15:12]), .eq(comparator_3_eq));  // open: gt, lt
  assign bit_extender_1_out = {{3{not_1_out}}, not_1_out};  // Bit_Extender bit_extender_1
  assign bit_extender_2_out = {{3{str}}, str};  // Bit_Extender bit_extender_2
  assign bit_extender_3_out = {{3{ld}}, ld};  // Bit_Extender bit_extender_3
  assign bit_extender_4_out = {{3{comparator_3_eq}}, comparator_3_eq};  // Bit_Extender bit_extender_4
  assign Else_out = Instruction[15:12] & bit_extender_1_out;  // AND_Gate Else, 4 bits wide
  assign _1011_out = bit_extender_2_out & 4'b0100;  // AND_Gate _1011, 4 bits wide
  assign _1010_out = bit_extender_3_out & 4'b0100;  // AND_Gate _1010, 4 bits wide
  assign _0001_out = bit_extender_4_out & Instruction[3:0];  // AND_Gate _0001, 4 bits wide
  assign or_2_out = _0001_out | _1010_out | _1011_out | Else_out;  // OR_Gate or_2, 4 bits wide
  Register_File_2_0 Register_file (
    .rs_in(Instruction[7:4]), .rt_in(multiplexer_1_out), .\input (multiplexer_2_out),
    .in_4(Instruction[11:8]), .clock(Clock), .reset(Reset), .write(write_out), .out_10(out_11),
    .out_11(out_13), .out_12(out_14), .out_13(out_15), .out_14(out_16), .out_15(out_17), .out_16(out_18),
    .out_17(out_19), .out_18(out_20), .out_19(out_21), .out_20(out_22), .out_21(out_23), .out_22(out_24),
    .out_23(out_25), .out_24(out_26), .out_25(out_27), .rs_content(Register_file_rs_content), .rt_content(D));
  assign bit_extender_5_out = {{4{1'b0}}, Instruction[3:0]};  // Bit_Extender bit_extender_5
  or imm (imm_out, ld, str);
  Multiplexer #(.width(8)) multiplexer_3 (
    .in0(D), .in1(bit_extender_5_out), .out(multiplexer_3_out), .sel(imm_out));  // open: en
  _8_bit_ALU u_8_bit_alu_1 (
    .ALU_code(or_2_out), .a(Register_file_rs_content), .b(multiplexer_3_out), .result(A), .overflow(Overflow));

  assign C = Clock;
  assign clr = Reset;

  // Notes on the sheet:
  //   op
  //   rs
  //   rd
  //   rt
  //   rs en rt
  //   Else -> use op as op code
  //   op add
  //   Opcode == 0001 -> use rt as op code
  //   Opcode == 1010 -> lb at position (rs+rt) to rd
  //   Opcode == 1011 -> sb at position rd to (rs+rt) 
  //   rt
  //   Resultaat vd ALU
  //   lb
  //   adress + offset
  //   rt
  //   gelezen lb
endmodule

module equal (
  input  [3:0] in_1,
  input  [3:0] in_2,
  output out_3
);

  wire and_1_out, and_2_out, and_3_out, and_4_out, not_1_out, not_2_out, not_3_out, not_4_out, or_1_out,
       or_2_out, or_3_out, or_4_out, or_5_out, or_6_out, or_7_out, or_8_out;

  or or_1 (or_1_out, in_1[0], in_2[0]);
  and and_1 (and_1_out, in_1[0], in_2[0]);
  or or_2 (or_2_out, in_1[1], in_2[1]);
  and and_2 (and_2_out, in_1[1], in_2[1]);
  or or_3 (or_3_out, in_1[2], in_2[2]);
  and and_3 (and_3_out, in_1[2], in_2[2]);
  or or_4 (or_4_out, in_2[3], in_1[3]);
  and and_4 (and_4_out, in_2[3], in_1[3]);
  not not_1 (not_1_out, or_1_out);
  or or_5 (or_5_out, not_1_out, and_1_out);
  not not_2 (not_2_out, or_2_out);
  or or_6 (or_6_out, not_2_out, and_2_out);
  not not_3 (not_3_out, or_3_out);
  or or_7 (or_7_out, not_3_out, and_3_out);
  not not_4 (not_4_out, or_4_out);
  or or_8 (or_8_out, not_4_out, and_4_out);
  and and_5 (out_3, or_5_out, or_6_out, or_7_out, or_8_out);
endmodule

module sign_add (
  input  [3:0] in_1,
  input  [7:0] in_2,
  output [7:0] out_3
);

  wire and_1_out, not_1_out, not_2_out, or_1_out, or_2_out;
  wire [7:0] adder_1_out, bit_extender_1_out, subtractor_1_out;

  assign bit_extender_1_out = {{4{in_1[3]}}, in_1};  // Bit_Extender bit_extender_1
  or or_1 (or_1_out, in_1[3], in_2[7]);
  not not_1 (not_1_out, or_1_out);
  or or_2 (or_2_out, not_1_out, and_1_out);
  and and_1 (and_1_out, in_1[3], in_2[7]);
  Adder adder_1 (.a(bit_extender_1_out), .b(in_2), .out(adder_1_out));  // open: cin, cout
  Subtractor subtractor_1 (.a(bit_extender_1_out), .b(in_2), .out(subtractor_1_out));  // open: bin, bout
  not not_2 (not_2_out, or_2_out);
  Multiplexer #(.width(8)) multiplexer_1 (
    .in0(adder_1_out), .in1(subtractor_1_out), .out(out_3), .sel(not_2_out));  // open: en

  // Notes on the sheet:
  //   doet add wanneer bij beide getallen de eerst dezelfde waarde heeft
  //   een neg met neg optellen geeft meer neg
  //   pos optellen met neg trekt het pos getal af van het neg
  //   neg optellen met pos trekt het neg getal af van het pos , heeft zelfde effect als hierboven
  //   checkt of eerste getal zxelfde is 
endmodule

module Control_Unit (
  input  [15:0] in_1,
  output ERROR__Unknown_Instruction,
  output Double_ALU,
  output Single_ALU,
  output lb,
  output sb,
  output ldi,
  output addi,
  output beq,
  output blt,
  output jal,
  output j,
  output jr,
  output Write_reg,
  output read_rd_from_reg_instead_of_rt__TODO__Remove,
  output [1:0] ALU_b__rt00_imm01_s10,
  output [1:0] register_store_ALUb00_DATA01_rs10,
  output absolute_instr,
  output rel_instr_possible,
  output reg_output_2_to_alu_a,
  output [3:0] rt,
  output [3:0] rs,
  output [3:0] rd,
  output [3:0] Opcode,
  output [3:0] opcode_2
);

  wire comparator_1_gt, comparator_2_lt, equal_1_out_3, equal_8_out_3, equal_9_out_3, equal_10_out_3,
       not_2_out, or_1_out, or_2_out, or_3_out;
  wire [3:0] and_6_out, and_7_out, and_8_out, and_9_out, and_10_out, and_11_out, bit_extender_1_out,
       bit_extender_2_out, bit_extender_3_out, bit_extender_4_out, bit_extender_5_out, bit_extender_6_out;

  not not_1 (Double_ALU, or_1_out);
  or or_1 (or_1_out, equal_1_out_3, lb, sb, ldi, addi, beq, ALU_b__rt00_imm01_s10[1]);
  equal equal_1 (.in_1(4'b0001), .in_2(in_1[15:12]), .out_3(equal_1_out_3));
  equal equal_2 (.in_1(4'b1010), .in_2(in_1[15:12]), .out_3(lb));
  equal equal_3 (.in_1(4'b1011), .in_2(in_1[15:12]), .out_3(sb));
  equal equal_4 (.in_1(4'b1100), .in_2(in_1[15:12]), .out_3(ldi));
  equal equal_5 (.in_1(4'b1101), .in_2(in_1[15:12]), .out_3(addi));
  equal equal_6 (.in_1(4'b1110), .in_2(in_1[15:12]), .out_3(beq));
  equal equal_7 (.in_1(4'b1111), .in_2(in_1[15:12]), .out_3(ALU_b__rt00_imm01_s10[1]));
  and and_1 (Single_ALU, not_2_out, equal_1_out_3);
  not not_2 (not_2_out, or_2_out);
  or or_2 (or_2_out, equal_8_out_3, equal_9_out_3, equal_10_out_3);
  equal equal_8 (.in_1(4'b0100), .in_2(in_1[3:0]), .out_3(equal_8_out_3));
  equal equal_9 (.in_1(4'b0011), .in_2(in_1[3:0]), .out_3(equal_9_out_3));
  equal equal_10 (.in_1(4'b0010), .in_2(in_1[3:0]), .out_3(equal_10_out_3));
  Comparator #(.width(4)) comparator_1 (.a(in_1[3:0]), .b(4'b0100), .gt(comparator_1_gt));  // open: eq, lt
  Comparator #(.width(4)) comparator_2 (.a(in_1[3:0]), .b(4'b1010), .lt(comparator_2_lt));  // open: gt, eq
  and and_2 (jal, equal_8_out_3, equal_1_out_3);
  and and_3 (addi, equal_9_out_3, equal_1_out_3);
  and and_4 (addi, equal_10_out_3, equal_1_out_3);
  and and_5 (ERROR__Unknown_Instruction, comparator_1_gt, comparator_2_lt, Single_ALU);
  assign bit_extender_1_out = {{3{Double_ALU}}, Double_ALU};  // Bit_Extender bit_extender_1
  assign bit_extender_2_out = {{3{Single_ALU}}, Single_ALU};  // Bit_Extender bit_extender_2
  assign bit_extender_3_out = {{3{or_3_out}}, or_3_out};  // Bit_Extender bit_extender_3
  or or_3 (or_3_out, lb, sb, addi);
  assign bit_extender_4_out = {{3{beq}}, beq};  // Bit_Extender bit_extender_4
  assign bit_extender_5_out = {{3{ALU_b__rt00_imm01_s10[1]}}, ALU_b__rt00_imm01_s10[1]};  // Bit_Extender bit_extender_5
  or or_4 (ALU_b__rt00_imm01_s10[0], addi, sb, lb, addi, addi, ldi);
  or or_5 (absolute_instr, addi, addi, jal);
  or or_6 (rel_instr_possible, ALU_b__rt00_imm01_s10[1], beq);
  assign bit_extender_6_out = {{3{ALU_b__rt00_imm01_s10[0]}}, ALU_b__rt00_imm01_s10[0]};  // Bit_Extender bit_extender_6
  assign and_6_out = bit_extender_1_out & in_1[15:12];  // AND_Gate and_6, 4 bits wide
  assign and_7_out = bit_extender_2_out & in_1[3:0];  // AND_Gate and_7, 4 bits wide
  assign and_8_out = bit_extender_3_out & 4'b0100;  // AND_Gate and_8, 4 bits wide
  assign and_9_out = bit_extender_4_out & 4'b1000;  // AND_Gate and_9, 4 bits wide
  assign and_10_out = bit_extender_5_out & 4'b0110;  // AND_Gate and_10, 4 bits wide
  or or_7 (Write_reg, Double_ALU, Single_ALU, lb, jal, ldi, addi, jal);
  or or_8 (read_rd_from_reg_instead_of_rt__TODO__Remove, ALU_b__rt00_imm01_s10[1], beq, sb, addi);
  assign register_store_ALUb00_DATA01_rs10 = {jal, lb} | {2{ldi}};  // OR_Gate or_9, 2 bits wide
  or or_10 (reg_output_2_to_alu_a, addi, ALU_b__rt00_imm01_s10[1]);
  assign and_11_out = 4'b0100 & bit_extender_6_out;  // AND_Gate and_11, 4 bits wide
  assign Opcode = and_11_out | and_6_out | and_7_out | and_8_out | and_9_out | and_10_out;  // OR_Gate or_11, 4 bits wide

  assign blt = ALU_b__rt00_imm01_s10[1];
  assign j = addi;
  assign jr = addi;
  assign opcode_2 = in_1[15:12];
  assign rd = in_1[11:8];
  assign rs = in_1[7:4];
  assign rt = in_1[3:0];

  // Notes on the sheet:
  //   Geen enkele van de onderstaande:
  //   Single ALU:
  //   lb:
  //   sb:
  //   ldi:
  //   addi:
  //   beq:
  //   blt:
  //   = Double ALU
  //   jal
  //   j
  //   jr
  //   Exceptions: op_code = 0001 en rt = [5, 9], alle andere instr worden gebruikt
  //   Double ALU
  //   Single ALU
  //   ALU add: lb, sb, addi
  //   TODO: Alle imm opcode 4
endmodule

module immidiate_unit (
  input  [3:0] rd,
  input  [3:0] rs,
  input  [3:0] rt,
  input  ldi,
  input  lb,
  input  sb,
  input  addi,
  input  beq,
  input  blt,
  input  jr,
  input  j,
  input  jal,
  output [7:0] out_13
);

  wire or_1_out, or_2_out, or_3_out;
  wire [7:0] and_1_out, and_2_out, and_3_out, and_4_out, and_5_out, bit_extender_1_out, bit_extender_2_out,
       bit_extender_3_out, bit_extender_4_out, bit_extender_5_out, bit_extender_6_out, bit_extender_7_out,
       bit_extender_8_out, or_5_out;

  or or_1 (or_1_out, lb, sb);
  or or_2 (or_2_out, addi, beq, blt);
  assign bit_extender_1_out = {{7{jr}}, jr};  // Bit_Extender bit_extender_1
  or or_3 (or_3_out, j, jal);
  assign bit_extender_2_out = {{7{or_1_out}}, or_1_out};  // Bit_Extender bit_extender_2
  assign bit_extender_3_out = {{7{or_2_out}}, or_2_out};  // Bit_Extender bit_extender_3
  assign bit_extender_4_out = {{7{or_3_out}}, or_3_out};  // Bit_Extender bit_extender_4
  assign bit_extender_5_out = {{4{1'b0}}, rt};  // Bit_Extender bit_extender_5
  assign bit_extender_6_out = {{4{rt[3]}}, rt};  // Bit_Extender bit_extender_6
  assign bit_extender_7_out = {{4{rs[3]}}, rs};  // Bit_Extender bit_extender_7
  assign and_1_out = bit_extender_7_out & bit_extender_1_out;  // AND_Gate and_1, 8 bits wide
  assign and_2_out = {rd, rs} & bit_extender_4_out;  // AND_Gate and_2, 8 bits wide
  assign and_3_out = bit_extender_5_out & bit_extender_2_out;  // AND_Gate and_3, 8 bits wide
  assign and_4_out = bit_extender_6_out & bit_extender_3_out;  // AND_Gate and_4, 8 bits wide
  assign bit_extender_8_out = {{7{ldi}}, ldi};  // Bit_Extender bit_extender_8
  assign and_5_out = {rs, rt} & bit_extender_8_out;  // AND_Gate and_5, 8 bits wide
  assign out_13 = and_5_out | or_5_out;  // OR_Gate or_4, 8 bits wide
  assign or_5_out = and_3_out | and_4_out | and_1_out | and_2_out;  // OR_Gate or_5, 8 bits wide
endmodule
